// Logisim project 07ABR-Somador.circ as structural Verilog: 6 circuits, main circuit main
module main (
  input  A,
  input  B,
  input  C,
  output C_out,
  output S
);

  wire and_1_out, and_2_out, and_3_out, xor_1_out;

  and and_1 (and_1_out, A, B);
  and and_2 (and_2_out, A, C);
  or or_1 (C_out, and_1_out, and_2_out, and_3_out);
  and and_3 (and_3_out, B, C);
  xor xor_1 (xor_1_out, B, C);
  xor xor_2 (S, xor_1_out, A);
endmodule

module somadorRippleCarry (
  input  [7:0] A,
  input  [7:0] B,
  input  in_3,
  output [7:0] S
);

  wire main_1_c_out, main_2_c_out, main_3_c_out, main_4_c_out, main_5_c_out, main_6_c_out, main_7_c_out,
       main_8_c_out;
  wire [7:0] xor_1_out;

  assign xor_1_out = B ^ {8{in_3}};  // XOR_Gate xor_1, 8 bits wide
  main main_1 (.C_out(main_1_c_out), .S(S[7]), .A(A[7]), .B(xor_1_out[7]), .C(main_2_c_out));
  main main_2 (.C_out(main_2_c_out), .S(S[6]), .A(A[6]), .B(xor_1_out[6]), .C(main_3_c_out));
  main main_3 (.C_out(main_3_c_out), .S(S[5]), .A(A[5]), .B(xor_1_out[5]), .C(main_4_c_out));
  main main_4 (.C_out(main_4_c_out), .S(S[4]), .A(A[4]), .B(xor_1_out[4]), .C(main_5_c_out));
  main main_5 (.C_out(main_5_c_out), .S(S[3]), .A(A[3]), .B(xor_1_out[3]), .C(main_6_c_out));
  main main_6 (.C_out(main_6_c_out), .S(S[2]), .A(A[2]), .B(xor_1_out[2]), .C(main_7_c_out));
  main main_7 (.C_out(main_7_c_out), .S(S[1]), .A(A[1]), .B(xor_1_out[1]), .C(main_8_c_out));
  main main_8 (.C_out(main_8_c_out), .S(S[0]), .A(A[0]), .B(xor_1_out[0]), .C(in_3));
endmodule

module somadorComCout (
  input  A,
  input  B,
  input  C,
  output C_out,
  output S
);

  wire and_1_out, and_2_out, and_3_out, xor_1_out;

  and and_1 (and_1_out, A, B);
  or or_1 (C_out, and_1_out, and_2_out, and_3_out);
  and and_2 (and_2_out, A, C);
  and and_3 (and_3_out, B, C);
  xor xor_1 (xor_1_out, B, C);
  xor xor_2 (S, xor_1_out, A);
endmodule

module somadorSemCout (
  input  A,
  input  B,
  input  C,
  output S
);

  wire xor_1_out;

  xor xor_1 (xor_1_out, C, B);
  xor xor_2 (S, xor_1_out, A);
endmodule

module somadorLookAhead (
  input  [7:0] A,
  input  [7:0] B,
  input  in_3,
  output [7:0] S
);

  wire and_1_out, and_2_out, and_3_out, and_4_out, and_5_out, and_6_out, and_7_out, and_8_out, and_9_out,
       and_10_out, and_11_out, and_12_out, and_13_out, and_14_out, and_15_out, and_16_out, and_17_out,
       and_18_out, and_19_out, and_20_out, and_21_out, and_22_out, and_23_out, and_24_out, and_25_out,
       and_26_out, and_27_out, and_28_out, G1_2_out, G1_out, G2_out, G3_out, G4_out, G5_out, G6_out, G7_out,
       or_1_out, or_2_out, or_3_out, or_4_out, or_5_out, or_6_out, or_7_out, P1_2_out, P1_out, P2_out,
       P3_out, P4_out, P5_out, P6_out, P7_out;
  wire [7:0] xor_1_out;

  assign xor_1_out = B ^ {8{in_3}};  // XOR_Gate xor_1, 8 bits wide
  and G1 (G1_out, A[0], xor_1_out[0]);
  and G1_2 (G1_2_out, A[1], xor_1_out[1]);
  or P1 (P1_out, A[0], xor_1_out[0]);
  or P1_2 (P1_2_out, A[1], xor_1_out[1]);
  or P2 (P2_out, A[2], xor_1_out[2]);
  and G2 (G2_out, A[2], xor_1_out[2]);
  and G3 (G3_out, A[3], xor_1_out[3]);
  or P3 (P3_out, A[3], xor_1_out[3]);
  and G4 (G4_out, A[4], xor_1_out[4]);
  or P4 (P4_out, A[4], xor_1_out[4]);
  and G5 (G5_out, A[5], xor_1_out[5]);
  or P5 (P5_out, A[5], xor_1_out[5]);
  or P6 (P6_out, A[6], xor_1_out[6]);
  and G6 (G6_out, A[6], xor_1_out[6]);
  or P7 (P7_out, A[7], xor_1_out[7]);
  and G7 (G7_out, A[7], xor_1_out[7]);
  somadorSemCout S0 (.S(S[0]), .A(A[0]), .B(xor_1_out[0]), .C(in_3));
  and and_1 (and_1_out, P1_out, in_3);
  or or_1 (or_1_out, G1_out, and_1_out);
  somadorSemCout S1 (.S(S[1]), .A(A[1]), .B(xor_1_out[1]), .C(or_1_out));
  somadorSemCout S2 (.S(S[2]), .A(A[2]), .B(xor_1_out[2]), .C(or_2_out));
  and and_2 (and_2_out, P1_out, P1_2_out, in_3);
  and and_3 (and_3_out, G1_out, P1_2_out);
  or or_2 (or_2_out, G1_2_out, and_3_out, and_2_out);
  somadorSemCout S3 (.S(S[3]), .A(A[3]), .B(xor_1_out[3]), .C(or_3_out));
  and and_4 (and_4_out, G1_2_out, P2_out);
  or or_3 (or_3_out, G2_out, and_4_out, and_6_out, and_5_out);
  and and_5 (and_5_out, P1_out, P1_2_out, P2_out, in_3);
  and and_6 (and_6_out, G1_out, P1_2_out, P2_out);
  and and_7 (and_7_out, G2_out, P3_out);
  or or_4 (or_4_out, G3_out, and_7_out, and_8_out, and_9_out, and_10_out);
  somadorSemCout S4 (.S(S[4]), .A(A[4]), .B(xor_1_out[4]), .C(or_4_out));
  and and_8 (and_8_out, G1_2_out, P2_out, P3_out);
  and and_9 (and_9_out, G1_out, P1_2_out, P2_out, P3_out);
  and and_10 (and_10_out, P1_out, P1_2_out, P2_out, P3_out, in_3);
  or or_5 (or_5_out, G4_out, and_11_out, and_12_out, and_13_out, and_14_out, and_15_out);
  somadorSemCout S5 (.S(S[5]), .A(A[5]), .B(xor_1_out[5]), .C(or_5_out));
  and and_11 (and_11_out, G3_out, P4_out);
  and and_12 (and_12_out, G2_out, P3_out, P4_out);
  and and_13 (and_13_out, G1_2_out, P2_out, P3_out, P4_out);
  and and_14 (and_14_out, G1_out, P1_2_out, P2_out, P3_out, P4_out);
  and and_15 (and_15_out, P1_out, P1_2_out, P2_out, P3_out, P4_out, in_3);
  somadorSemCout S6 (.S(S[6]), .A(A[6]), .B(xor_1_out[6]), .C(or_6_out));
  and and_16 (and_16_out, G3_out, P4_out, P5_out);
  and and_17 (and_17_out, G4_out, P5_out);
  or or_6 (or_6_out, G5_out, and_17_out, and_16_out, and_18_out, and_19_out, and_20_out, and_21_out);
  and and_18 (and_18_out, G2_out, P3_out, P4_out, P5_out);
  and and_19 (and_19_out, G1_2_out, P2_out, P3_out, P4_out, P5_out);
  and and_20 (and_20_out, G1_out, P1_2_out, P2_out, P3_out, P4_out, P5_out);
  and and_21 (and_21_out, P1_out, P1_2_out, P2_out, P3_out, P4_out, P5_out, in_3);
  somadorSemCout S7 (.S(S[7]), .A(A[7]), .B(xor_1_out[7]), .C(or_7_out));
  and and_22 (and_22_out, G5_out, P6_out);
  or or_7 (or_7_out, G6_out, and_22_out, and_23_out, and_25_out, and_24_out, and_26_out, and_27_out, and_28_out);
  and and_23 (and_23_out, G4_out, P5_out, P6_out);
  and and_24 (and_24_out, G2_out, P3_out, P4_out, P5_out, P6_out);
  and and_25 (and_25_out, G3_out, P4_out, P5_out, P6_out);
  and and_26 (and_26_out, G1_2_out, P2_out, P3_out, P4_out, P5_out, P6_out);
  and and_27 (and_27_out, G1_out, P1_2_out, P2_out, P3_out, P4_out, P5_out, P6_out);
  and and_28 (and_28_out, P1_out, P1_2_out, P2_out, P3_out, P4_out, P5_out, P6_out, in_3);

  // Notes on the sheet:
  //   C out 0
  //   C out 1
  //   C out 2
  //   C out 3
  //   C out 4
  //   C out 5
  //   C out 6
endmodule

module versaoBoaAqui (
);

  wire and_1_out, and_2_out, and_3_out, and_4_out, and_5_out, and_6_out, and_7_out, or_1_out, S7_s, undriven,
       undriven_2, undriven_3, undriven_4, undriven_5, undriven_6, undriven_7, undriven_8, undriven_9,
       undriven_10, undriven_11, undriven_12, undriven_13, undriven_14, undriven_15, undriven_16, undriven_17;

  and and_1 (and_1_out, undriven_4, undriven_5);
  or or_1 (or_1_out, undriven_3, and_1_out, and_2_out, and_3_out, and_4_out, and_5_out, and_6_out, and_7_out);
  somadorSemCout S7 (.S(S7_s), .A(undriven), .B(undriven_2), .C(or_1_out));
  and and_2 (and_2_out, undriven_6, undriven_7, undriven_5);
  and and_3 (and_3_out, undriven_8, undriven_9, undriven_7, undriven_5);
  and and_4 (and_4_out, undriven_10, undriven_11, undriven_9, undriven_7, undriven_5);
  and and_5 (and_5_out, undriven_12, undriven_13, undriven_11, undriven_9, undriven_7, undriven_5);
  and and_6 (and_6_out, undriven_14, undriven_15, undriven_13, undriven_11, undriven_9, undriven_7, undriven_5);
  and and_7 (and_7_out, undriven_16, undriven_15, undriven_13, undriven_11, undriven_9, undriven_7, undriven_5, undriven_17);
endmodule
