// Logisim project 07ABR.circ as structural Verilog: 4 circuits, main circuit main
module main (
  input  A,
  input  B,
  input  C,
  output C_out,
  output S
);

  wire and_1_out, and_2_out, and_3_out, xor_1_out;

  and and_1 (and_1_out, A, B);
  or or_1 (C_out, and_1_out, and_2_out, and_3_out);
  and and_2 (and_2_out, A, C);
  and and_3 (and_3_out, B, C);
  xor xor_1 (xor_1_out, B, C);
  xor xor_2 (S, xor_1_out, A);
endmodule

module somador (
  input  [7:0] A,
  input  [7:0] B,
  input  in_3,
  output [7:0] S
);

  wire main_1_s, main_2_s, main_3_s, main_4_s, main_5_s, main_6_s, main_7_s, main_8_s;
  wire [7:0] xor_1_out;

  assign xor_1_out = B ^ {8{in_3}};  // XOR_Gate xor_1, 8 bits wide
  main main_1 (.C_out(S[7]), .S(main_1_s), .A(A[7]), .B(xor_1_out[7]), .C(main_2_s));
  main main_2 (.C_out(S[6]), .S(main_2_s), .A(A[6]), .B(xor_1_out[6]), .C(main_3_s));
  main main_3 (.C_out(S[5]), .S(main_3_s), .A(A[5]), .B(xor_1_out[5]), .C(main_4_s));
  main main_4 (.C_out(S[4]), .S(main_4_s), .A(A[4]), .B(xor_1_out[4]), .C(main_5_s));
  main main_5 (.C_out(S[3]), .S(main_5_s), .A(A[3]), .B(xor_1_out[3]), .C(main_6_s));
  main main_6 (.C_out(S[2]), .S(main_6_s), .A(A[2]), .B(xor_1_out[2]), .C(main_7_s));
  main main_7 (.C_out(S[1]), .S(main_7_s), .A(A[1]), .B(xor_1_out[1]), .C(main_8_s));
  main main_8 (.C_out(S[0]), .S(main_8_s), .A(A[0]), .B(xor_1_out[0]), .C(in_3));
endmodule

module somadorComCout (
  input  A,
  input  B,
  input  C,
  output C_out,
  output S
);

  wire and_1_out, and_2_out, and_3_out, xor_1_out;

  and and_1 (and_1_out, A, B);
  and and_2 (and_2_out, A, C);
  or or_1 (C_out, and_1_out, and_2_out, and_3_out);
  and and_3 (and_3_out, B, C);
  xor xor_1 (xor_1_out, B, C);
  xor xor_2 (S, xor_1_out, A);
endmodule

module somadorSemCout (
  input  A,
  input  B,
  input  C,
  output S
);

  wire xor_1_out;

  xor xor_1 (xor_1_out, B, C);
  xor xor_2 (S, xor_1_out, A);
endmodule
