// Logisim project 12MAI - Contador.circ as structural Verilog
module Circuito_RS (
);

  wire and_1_out, and_2_out, and_3_out, and_4_out, clock_1_out, j_k_ff_1_qn, j_k_ff_2_qn, j_k_ff_3_qn,
       j_k_ff_4_qn, j_k_ff_5_qn, j_k_ff_6_qn, j_k_ff_7_qn, j_k_ff_8_qn, j_k_ff_9_qn, j_k_ff_10_qn,
       j_k_ff_11_qn, j_k_ff_12_qn, j_k_ff_13_qn, j_k_ff_14_qn, j_k_ff_15_qn, j_k_ff_16_qn, Q0, Q1, Q2, Q3,
       Q20, Q21, Q22, Q23, Q30, Q31, Q32, Q33, Q40, Q41, Q42, Q43;

  and and_1 (and_1_out, Q3, ~Q2, Q1, ~Q0);  // AND_Gate
  J_K_Flip_Flop #(.trigger("falling")) j_k_ff_1 (
    .J(1'b1), .clk(clock_1_out), .K(1'b1), .Q(Q0), .Qn(j_k_ff_1_qn), .reset(and_1_out));  // open: preset, en
  Clock clock_1 (.out(clock_1_out));
  Hex_Digit_Display hex_digit_display_1 (.value({Q23, Q22, Q21, Q20}));  // open: dp
  J_K_Flip_Flop #(.trigger("falling")) j_k_ff_2 (
    .J(1'b1), .clk(Q0), .K(1'b1), .Q(Q1), .Qn(j_k_ff_2_qn), .reset(and_1_out));  // open: preset, en
  Hex_Digit_Display hex_digit_display_2 (.value({Q3, Q2, Q1, Q0}));  // open: dp
  J_K_Flip_Flop #(.trigger("falling")) j_k_ff_3 (
    .J(1'b1), .clk(Q1), .K(1'b1), .Q(Q2), .Qn(j_k_ff_3_qn), .reset(and_1_out));  // open: preset, en
  J_K_Flip_Flop #(.trigger("falling")) j_k_ff_4 (
    .J(1'b1), .clk(Q2), .K(1'b1), .Q(Q3), .Qn(j_k_ff_4_qn), .reset(and_1_out));  // open: preset, en
  and and_2 (and_2_out, ~Q23, Q22, Q21, ~Q20);  // AND_Gate
  J_K_Flip_Flop #(.trigger("falling")) j_k_ff_5 (
    .J(1'b1), .clk(Q3), .K(1'b1), .Q(Q20), .Qn(j_k_ff_5_qn), .reset(and_2_out));  // open: preset, en
  Hex_Digit_Display hex_digit_display_3 (.value({Q43, Q42, Q41, Q40}));  // open: dp
  J_K_Flip_Flop #(.trigger("falling")) j_k_ff_6 (
    .J(1'b1), .clk(Q20), .K(1'b1), .Q(Q21), .Qn(j_k_ff_6_qn), .reset(and_2_out));  // open: preset, en
  Hex_Digit_Display hex_digit_display_4 (.value({Q33, Q32, Q31, Q30}));  // open: dp
  J_K_Flip_Flop #(.trigger("falling")) j_k_ff_7 (
    .J(1'b1), .clk(Q21), .K(1'b1), .Q(Q22), .Qn(j_k_ff_7_qn), .reset(and_2_out));  // open: preset, en
  J_K_Flip_Flop #(.trigger("falling")) j_k_ff_8 (
    .J(1'b1), .clk(Q22), .K(1'b1), .Q(Q23), .Qn(j_k_ff_8_qn), .reset(and_2_out));  // open: preset, en
  Hex_Digit_Display hex_digit_display_5 (.value({Q23, Q22, Q21, Q20}));  // open: dp
  and and_3 (and_3_out, Q3, ~Q2, Q1, ~Q0);  // AND_Gate
  J_K_Flip_Flop #(.trigger("falling")) j_k_ff_9 (
    .J(1'b1), .clk(Q23), .K(1'b1), .Q(Q30), .Qn(j_k_ff_9_qn), .reset(and_3_out));  // open: preset, en
  Hex_Digit_Display hex_digit_display_6 (.value({Q3, Q2, Q1, Q0}));  // open: dp
  J_K_Flip_Flop #(.trigger("falling")) j_k_ff_10 (
    .J(1'b1), .clk(Q30), .K(1'b1), .Q(Q31), .Qn(j_k_ff_10_qn), .reset(and_3_out));  // open: preset, en
  J_K_Flip_Flop #(.trigger("falling")) j_k_ff_11 (
    .J(1'b1), .clk(Q31), .K(1'b1), .Q(Q32), .Qn(j_k_ff_11_qn), .reset(and_3_out));  // open: preset, en
  and and_4 (and_4_out, ~Q23, Q22, Q21, ~Q20);  // AND_Gate
  J_K_Flip_Flop #(.trigger("falling")) j_k_ff_12 (
    .J(1'b1), .clk(Q32), .K(1'b1), .Q(Q33), .Qn(j_k_ff_12_qn), .reset(and_3_out));  // open: preset, en
  J_K_Flip_Flop #(.trigger("falling")) j_k_ff_13 (
    .J(1'b1), .clk(Q33), .K(1'b1), .Q(Q40), .Qn(j_k_ff_13_qn), .reset(and_4_out));  // open: preset, en
  J_K_Flip_Flop #(.trigger("falling")) j_k_ff_14 (
    .J(1'b1), .clk(Q40), .K(1'b1), .Q(Q41), .Qn(j_k_ff_14_qn), .reset(and_4_out));  // open: preset, en
  J_K_Flip_Flop #(.trigger("falling")) j_k_ff_15 (
    .J(1'b1), .clk(Q41), .K(1'b1), .Q(Q42), .Qn(j_k_ff_15_qn), .reset(and_4_out));  // open: preset, en
  J_K_Flip_Flop #(.trigger("falling")) j_k_ff_16 (
    .J(1'b1), .clk(Q42), .K(1'b1), .Q(Q43), .Qn(j_k_ff_16_qn), .reset(and_4_out));  // open: preset, en
endmodule

module Contador22a3 (
);

  wire and_1_out, and_2_out, clock_1_out, j_k_ff_1_qn, j_k_ff_2_qn, j_k_ff_3_qn, j_k_ff_4_qn, j_k_ff_5_qn,
       j_k_ff_6_qn, j_k_ff_7_qn, j_k_ff_8_qn, Q0, Q1, Q2, Q3, Q20, Q21, Q22, Q23;

  and and_1 (and_1_out, Q3, Q2, Q1, Q0);
  J_K_Flip_Flop #(.trigger("falling")) j_k_ff_1 (
    .J(1'b1), .clk(clock_1_out), .K(1'b1), .Q(Q0), .Qn(j_k_ff_1_qn), .reset(and_1_out));  // open: preset, en
  Clock clock_1 (.out(clock_1_out));
  Hex_Digit_Display hex_digit_display_1 (.value({Q23, Q22, Q21, Q20}));  // open: dp
  J_K_Flip_Flop #(.trigger("falling")) j_k_ff_2 (
    .J(1'b1), .clk(Q0), .K(1'b1), .Q(Q1), .Qn(j_k_ff_2_qn), .reset(and_1_out));  // open: preset, en
  Hex_Digit_Display hex_digit_display_2 (.value({Q3, Q2, Q1, Q0}));  // open: dp
  J_K_Flip_Flop #(.trigger("falling")) j_k_ff_3 (
    .J(1'b1), .clk(Q1), .K(1'b1), .Q(Q2), .Qn(j_k_ff_3_qn), .reset(and_1_out));  // open: preset, en
  J_K_Flip_Flop #(.trigger("falling")) j_k_ff_4 (
    .J(1'b1), .clk(Q2), .K(1'b1), .Q(Q3), .Qn(j_k_ff_4_qn), .reset(and_1_out));  // open: preset, en
  and and_2 (and_2_out, ~Q23, Q22, Q21, ~Q20);  // AND_Gate
  J_K_Flip_Flop #(.trigger("falling")) j_k_ff_5 (
    .J(1'b1), .clk(Q3), .K(1'b1), .Q(Q20), .Qn(j_k_ff_5_qn), .reset(and_2_out));  // open: preset, en
  J_K_Flip_Flop #(.trigger("falling")) j_k_ff_6 (
    .J(1'b1), .clk(Q20), .K(1'b1), .Q(Q21), .Qn(j_k_ff_6_qn), .reset(and_2_out));  // open: preset, en
  J_K_Flip_Flop #(.trigger("falling")) j_k_ff_7 (
    .J(1'b1), .clk(Q21), .K(1'b1), .Q(Q22), .Qn(j_k_ff_7_qn), .reset(and_2_out));  // open: preset, en
  J_K_Flip_Flop #(.trigger("falling")) j_k_ff_8 (
    .J(1'b1), .clk(Q22), .K(1'b1), .Q(Q23), .Qn(j_k_ff_8_qn), .reset(and_2_out));  // open: preset, en
endmodule

module Contador22a3comT (
  output [4:0] out_1,
  output [4:0] out_2,
  output [7:0] out_3
);

  wire and_1_out, clock_1_out;
  wire [7:0] divider_1_out, divider_1_rem;

  Clock clock_1 (.out(clock_1_out));
  T_Flip_Flop t_ff_1 (.clk(clock_1_out), .T(1'b1), .Q(out_1[0]), .reset(and_1_out));  // open: Qn, preset, en
  T_Flip_Flop t_ff_2 (.clk(out_1[1]), .T(1'b1), .Q(out_1[2]), .preset(and_1_out));  // open: Qn, reset, en
  T_Flip_Flop t_ff_3 (.clk(out_1[0]), .T(1'b1), .Q(out_1[1]), .preset(and_1_out));  // open: Qn, reset, en
  Hex_Digit_Display hex_digit_display_1 (.value(divider_1_out[3:0]));  // open: dp
  Divider divider_1 (.a({3'b000, out_1}), .b(8'ha), .out(divider_1_out), .rem(divider_1_rem));  // open: upper
  T_Flip_Flop t_ff_4 (.clk(out_1[2]), .T(1'b1), .Q(out_1[3]), .reset(and_1_out));  // open: Qn, preset, en
  Hex_Digit_Display hex_digit_display_2 (.value(divider_1_rem[3:0]));  // open: dp
  T_Flip_Flop t_ff_5 (.clk(out_1[3]), .T(1'b1), .Q(out_1[4]), .preset(and_1_out));  // open: Qn, reset, en
  and and_1 (and_1_out, ~out_1[4], ~out_1[3], ~out_1[2], out_1[1], ~out_1[0]);  // AND_Gate

  assign out_2 = out_1;
  assign out_3 = {3'b000, out_1};
endmodule
