// Logisim project 20ABR-Multiplicador.circ as structural Verilog: 3 circuits, main circuit main
module main (
  input  A2,
  input  A1,
  input  A0,
  input  B2,
  input  B1,
  input  B0,
  output out_7,
  output out_8,
  output out_9,
  output out_10,
  output out_11,
  output out_12
);

  wire and_1_out, and_2_out, and_3_out, and_4_out, and_5_out, and_6_out, and_7_out, and_8_out,
       fulladder_2_cout, fulladder_2_s, fulladder_3_cout, halfadder_1_cout, halfadder_1_s, halfadder_2_cout,
       halfadder_3_cout;

  Hex_Digit_Display hex_digit_display_1 (.value({1'b0, A2, A1, A0}));  // open: dp
  Hex_Digit_Display hex_digit_display_2 (.value({1'b0, B2, B1, B0}));  // open: dp
  and and_1 (and_1_out, A2, B2);
  and and_2 (and_2_out, A2, B1);
  HalfAdder halfadder_1 (.A(and_2_out), .B(fulladder_2_cout), .S(halfadder_1_s), .Cout(halfadder_1_cout));
  and and_3 (and_3_out, A1, B2);
  FullAdder fulladder_1 (.A(and_1_out), .B(halfadder_1_cout), .Cin(fulladder_3_cout), .S(out_9), .Cout(out_8));
  and and_4 (and_4_out, A2, B0);
  and and_5 (and_5_out, A1, B1);
  FullAdder fulladder_2 (
    .A(and_5_out), .B(and_4_out), .Cin(halfadder_3_cout), .S(fulladder_2_s), .Cout(fulladder_2_cout));
  and and_6 (and_6_out, A0, B2);
  HalfAdder halfadder_2 (.A(and_6_out), .B(fulladder_2_s), .S(out_11), .Cout(halfadder_2_cout));
  FullAdder fulladder_3 (.A(and_3_out), .B(halfadder_1_s), .Cin(halfadder_2_cout), .S(out_10), .Cout(fulladder_3_cout));
  and and_7 (and_7_out, A1, B0);
  and and_8 (and_8_out, A0, B1);
  HalfAdder halfadder_3 (.A(and_8_out), .B(and_7_out), .S(out_12), .Cout(halfadder_3_cout));
  and and_9 (out_7, A0, B0);

  // Notes on the sheet:
  //   X
endmodule

module FullAdder (
  input  A,
  input  B,
  input  Cin,
  output S,
  output Cout
);

  wire and_1_out, and_2_out, and_3_out, and_4_out, and_5_out, and_6_out, not_1_out, not_2_out, not_3_out,
       not_4_out, not_5_out, not_6_out;

  not not_1 (not_1_out, A);
  not not_2 (not_2_out, B);
  not not_3 (not_3_out, A);
  not not_4 (not_4_out, Cin);
  not not_5 (not_5_out, B);
  not not_6 (not_6_out, Cin);
  and and_1 (and_1_out, A, Cin);
  and and_2 (and_2_out, A, B);
  and and_3 (and_3_out, not_1_out, not_2_out, Cin);
  and and_4 (and_4_out, not_3_out, B, not_4_out);
  and and_5 (and_5_out, A, not_5_out, not_6_out);
  and and_6 (and_6_out, A, B, Cin);
  or or_1 (Cout, and_1_out, and_2_out);
  or or_2 (S, and_3_out, and_4_out, and_5_out, and_6_out);
endmodule

module HalfAdder (
  input  A,
  input  B,
  output S,
  output Cout
);

  wire and_2_out, and_3_out, not_1_out, not_2_out;

  not not_1 (not_1_out, A);
  not not_2 (not_2_out, B);
  and and_1 (Cout, A, B);
  and and_2 (and_2_out, not_1_out, B);
  and and_3 (and_3_out, A, not_2_out);
  or or_1 (S, and_2_out, and_3_out);
endmodule
