// Logisim project 8-2-22-1-3-12-14.circ as structural Verilog
module main (
);

  wire clock_1_out;

  Clock clock_1 (.out(clock_1_out));
  J_K_Flip_Flop F4 (.clk(clock_1_out));  // open: J, K, Q, Qn, preset, en, reset
  J_K_Flip_Flop F3 (.clk(clock_1_out));  // open: J, K, Q, Qn, preset, en, reset
  J_K_Flip_Flop F2 (.clk(clock_1_out));  // open: J, K, Q, Qn, preset, en, reset
  J_K_Flip_Flop F1 (.clk(clock_1_out));  // open: J, K, Q, Qn, preset, en, reset
  J_K_Flip_Flop F0 (.clk(clock_1_out));  // open: J, K, Q, Qn, preset, en, reset
endmodule

module _8_2_22_1_3_12_14 (
);

  wire clock_1_out, J0, J2, J3, J4, K1, K3, not_1_out, not_2_out, Q0, Q2, Q3;
  wire [7:0] divider_1_out, divider_1_rem;

  not not_1 (not_1_out, Q3);
  not not_2 (not_2_out, Q0);
  and and_1 (J3, J2, Q0);
  not not_3 (K3, Q2);
  or or_1 (K1, Q0, Q2);
  and and_2 (J4, not_1_out, not_2_out);
  Clock clock_1 (.out(clock_1_out));
  J_K_Flip_Flop F4 (.J(J4), .clk(clock_1_out), .K(1'b1), .Q(J0));  // open: Qn, preset, en, reset
  J_K_Flip_Flop F3 (.J(J3), .clk(clock_1_out), .K(K3), .Q(Q3));  // open: Qn, preset, en, reset
  Hex_Digit_Display hex_digit_display_1 (.value(divider_1_out[3:0]));  // open: dp
  Divider divider_1 (
    .a({3'b000, J0, Q3, Q2, J2, Q0}), .b(8'ha), .out(divider_1_out), .rem(divider_1_rem));  // open: upper
  J_K_Flip_Flop F2 (.J(J2), .clk(clock_1_out), .K(J2), .Q(Q2));  // open: Qn, preset, en, reset
  Hex_Digit_Display hex_digit_display_2 (.value(divider_1_rem[3:0]));  // open: dp
  J_K_Flip_Flop F1 (.J(1'b1), .clk(clock_1_out), .K(K1), .Q(J2));  // open: Qn, preset, en, reset
  J_K_Flip_Flop F0 (.J(J0), .clk(clock_1_out), .K(J2), .Q(Q0));  // open: Qn, preset, en, reset

  // Other names for the same wires on the sheet: K0 = J2; K2 = J2; Q1 = J2; Q4 = J0
endmodule
