// Logisim project DIVISOR.circ as structural Verilog: 3 circuits, main circuit main
module main (
  input  A,
  input  B,
  input  C,
  output s
);

  wire xor_1_out;

  xor xor_1 (xor_1_out, B, C);
  xor xor_2 (s, xor_1_out, A);
endmodule

module Somador (
  input  [7:0] A,
  input  [7:0] B,
  input  C,
  output [7:0] out_4,
  output out_5
);

  wire and_1_out, and_2_out, and_3_out, and_4_out, and_5_out, and_6_out, and_7_out, and_8_out, and_9_out,
       and_10_out, and_11_out, and_12_out, and_13_out, and_14_out, and_15_out, and_16_out, and_17_out,
       and_18_out, and_19_out, and_20_out, and_21_out, and_22_out, and_23_out, and_24_out, and_25_out,
       and_26_out, and_27_out, and_28_out, G1_out, G2_out, G3_out, G4_out, G5_out, G6_out, GO_out, or_1_out,
       or_2_out, or_3_out, or_4_out, or_5_out, or_6_out, or_7_out, P0_out, P1_out, P2_out, P3_out, P4_out,
       P5_out, P6_out;
  wire [7:0] xor_1_out;

  assign xor_1_out = B ^ {8{C}};  // XOR_Gate xor_1, 8 bits wide
  and GO (GO_out, A[0], xor_1_out[0]);
  or P0 (P0_out, A[0], xor_1_out[0]);
  or P1 (P1_out, A[1], xor_1_out[1]);
  and G1 (G1_out, A[1], xor_1_out[1]);
  and G2 (G2_out, A[2], xor_1_out[2]);
  or P2 (P2_out, A[2], xor_1_out[2]);
  or P3 (P3_out, A[3], xor_1_out[3]);
  and G3 (G3_out, A[3], xor_1_out[3]);
  and G4 (G4_out, A[4], xor_1_out[4]);
  or P4 (P4_out, A[4], xor_1_out[4]);
  or P5 (P5_out, A[5], xor_1_out[5]);
  and G5 (G5_out, A[5], xor_1_out[5]);
  or P6 (P6_out, A[6], xor_1_out[6]);
  and G6 (G6_out, A[6], xor_1_out[6]);
  main S0 (.s(out_4[0]), .A(A[0]), .B(C), .C(xor_1_out[0]));
  and and_1 (and_1_out, P0_out, C);
  or or_1 (or_1_out, GO_out, and_1_out);
  main S1 (.s(out_4[1]), .A(A[1]), .B(or_1_out), .C(xor_1_out[1]));
  main S2 (.s(out_4[2]), .A(A[2]), .B(or_2_out), .C(xor_1_out[2]));
  and and_2 (and_2_out, GO_out, P1_out);
  and and_3 (and_3_out, P0_out, P1_out, C);
  or or_2 (or_2_out, G1_out, and_2_out, and_3_out);
  and and_4 (and_4_out, G1_out, P2_out);
  main S3 (.s(out_4[3]), .A(A[3]), .B(or_3_out), .C(xor_1_out[3]));
  and and_5 (and_5_out, P0_out, P1_out, P2_out, C);
  and and_6 (and_6_out, GO_out, P1_out, P2_out);
  or or_3 (or_3_out, G2_out, and_4_out, and_6_out, and_5_out);
  main S4 (.s(out_4[4]), .A(A[4]), .B(or_4_out), .C(xor_1_out[4]));
  and and_7 (and_7_out, G1_out, P2_out, P3_out);
  and and_8 (and_8_out, G2_out, P3_out);
  and and_9 (and_9_out, GO_out, P1_out, P2_out, P3_out);
  and and_10 (and_10_out, P0_out, P1_out, P2_out, P3_out, C);
  or or_4 (or_4_out, G2_out, and_8_out, and_7_out, and_9_out, and_10_out);
  and and_11 (and_11_out, G3_out, P4_out);
  main S5 (.s(out_4[5]), .A(A[5]), .B(or_5_out), .C(xor_1_out[5]));
  and and_12 (and_12_out, G2_out, P3_out, P4_out);
  and and_13 (and_13_out, G1_out, P2_out, P3_out, P4_out);
  and and_14 (and_14_out, GO_out, P1_out, P2_out, P3_out, P4_out);
  or or_5 (or_5_out, G4_out, and_11_out, and_12_out, and_13_out, and_14_out, and_15_out);
  and and_15 (and_15_out, P0_out, P1_out, P2_out, P3_out, P4_out, C);
  main S6 (.s(out_4[6]), .A(A[6]), .B(or_6_out), .C(xor_1_out[6]));
  and and_16 (and_16_out, G4_out, P5_out);
  and and_17 (and_17_out, G3_out, P4_out, P5_out);
  and and_18 (and_18_out, G2_out, P3_out, P4_out, P5_out);
  and and_19 (and_19_out, G1_out, P2_out, P3_out, P4_out, P5_out);
  and and_20 (and_20_out, GO_out, P1_out, P2_out, P3_out, P4_out, P5_out);
  and and_21 (and_21_out, P0_out, P1_out, P2_out, P3_out, P4_out, P5_out, C);
  or or_6 (or_6_out, G5_out, and_16_out, and_17_out, and_18_out, and_19_out, and_20_out, and_21_out);
  and and_22 (and_22_out, G5_out, P6_out);
  main S7 (.s(out_4[7]), .A(A[7]), .B(or_7_out), .C(xor_1_out[7]));
  and and_23 (and_23_out, G4_out, P5_out, P6_out);
  and and_24 (and_24_out, G3_out, P4_out, P5_out, P6_out);
  and and_25 (and_25_out, G2_out, P3_out, P4_out, P5_out, P6_out);
  and and_26 (and_26_out, G1_out, P2_out, P3_out, P4_out, P5_out, P6_out);
  and and_27 (and_27_out, GO_out, P1_out, P2_out, P3_out, P4_out, P5_out, P6_out);
  and and_28 (and_28_out, P0_out, P1_out, P2_out, P3_out, P4_out, P5_out, P6_out, C);
  or or_7 (or_7_out, G6_out, and_22_out, and_23_out, and_24_out, and_25_out, and_26_out, and_27_out, and_28_out);

  assign out_5 = out_4[7];
endmodule

module Divisor (
  input  [7:0] DIVIDENDO,
  input  [7:0] DIVISOR,
  output [7:0] RESTO,
  output [7:0] QUOCIENTE
);

  wire _0, _1, _2, _3, _4, _5, _6, _7;
  wire [7:0] multiplexer_1_out, multiplexer_2_out, multiplexer_3_out, multiplexer_4_out, multiplexer_5_out,
       multiplexer_6_out, multiplexer_7_out, somador_1_out_4, somador_2_out_4, somador_3_out_4,
       somador_4_out_4, somador_5_out_4, somador_6_out_4, somador_7_out_4, somador_8_out_4;

  not not_1 (QUOCIENTE[0], _0);
  not not_2 (QUOCIENTE[1], _1);
  not not_3 (QUOCIENTE[2], _2);
  not not_4 (QUOCIENTE[3], _3);
  not not_5 (QUOCIENTE[4], _4);
  not not_6 (QUOCIENTE[5], _5);
  not not_7 (QUOCIENTE[6], _6);
  not not_8 (QUOCIENTE[7], _7);
  Somador somador_1 (.A({{7{1'b0}}, DIVIDENDO[7]}), .B(DIVISOR), .C(1'b1), .out_4(somador_1_out_4), .out_5(_7));
  Multiplexer #(.width(8), .enable("false")) multiplexer_1 (
    .in0(somador_1_out_4), .in1({{7{1'b0}}, DIVIDENDO[7]}), .out(multiplexer_1_out), .sel(_7));
  Somador somador_2 (
    .A({multiplexer_1_out[6:0], DIVIDENDO[6]}), .B(DIVISOR), .C(1'b1), .out_4(somador_2_out_4), .out_5(_6));
  Multiplexer #(.width(8), .enable("false")) multiplexer_2 (
    .in0(somador_2_out_4), .in1({multiplexer_1_out[6:0], DIVIDENDO[6]}), .out(multiplexer_2_out), .sel(_6));
  Multiplexer #(.width(8), .enable("false")) multiplexer_3 (
    .in0(somador_3_out_4), .in1({multiplexer_2_out[6:0], DIVIDENDO[5]}), .out(multiplexer_3_out), .sel(_5));
  Somador somador_3 (
    .A({multiplexer_2_out[6:0], DIVIDENDO[5]}), .B(DIVISOR), .C(1'b1), .out_4(somador_3_out_4), .out_5(_5));
  Somador somador_4 (
    .A({multiplexer_3_out[6:0], DIVIDENDO[4]}), .B(DIVISOR), .C(1'b1), .out_4(somador_4_out_4), .out_5(_4));
  Multiplexer #(.width(8), .enable("false")) multiplexer_4 (
    .in0(somador_4_out_4), .in1({multiplexer_3_out[6:0], DIVIDENDO[4]}), .out(multiplexer_4_out), .sel(_4));
  Somador somador_5 (
    .A({multiplexer_4_out[6:0], DIVIDENDO[3]}), .B(DIVISOR), .C(1'b1), .out_4(somador_5_out_4), .out_5(_3));
  Multiplexer #(.width(8), .enable("false")) multiplexer_5 (
    .in0(somador_5_out_4), .in1({multiplexer_4_out[6:0], DIVIDENDO[3]}), .out(multiplexer_5_out), .sel(_3));
  Somador somador_6 (
    .A({multiplexer_5_out[6:0], DIVIDENDO[2]}), .B(DIVISOR), .C(1'b1), .out_4(somador_6_out_4), .out_5(_2));
  Multiplexer #(.width(8), .enable("false")) multiplexer_6 (
    .in0(somador_6_out_4), .in1({multiplexer_5_out[6:0], DIVIDENDO[2]}), .out(multiplexer_6_out), .sel(_2));
  Somador somador_7 (
    .A({multiplexer_6_out[6:0], DIVIDENDO[1]}), .B(DIVISOR), .C(1'b1), .out_4(somador_7_out_4), .out_5(_1));
  Multiplexer #(.width(8), .enable("false")) multiplexer_7 (
    .in0(somador_7_out_4), .in1({multiplexer_6_out[6:0], DIVIDENDO[1]}), .out(multiplexer_7_out), .sel(_1));
  Somador somador_8 (
    .A({multiplexer_7_out[6:0], DIVIDENDO[0]}), .B(DIVISOR), .C(1'b1), .out_4(somador_8_out_4), .out_5(_0));
  Multiplexer #(.width(8), .enable("false")) multiplexer_8 (
    .in0(somador_8_out_4), .in1({multiplexer_7_out[6:0], DIVIDENDO[0]}), .out(RESTO), .sel(_0));

  // Other names for the same wires on the sheet: D[7:0] = DIVIDENDO; DV[7:0] = DIVISOR; Q[7:0] = QUOCIENTE;
  //   R[7:0] = RESTO
endmodule
