// Logisim project MEMORIA02jun2022.circ as structural Verilog
module \memória  (
  input  [7:0] \CONTEÚDO_A_SER_ESCRITO ,
  input  [2:0] \ENDEREÇO ,
  input  W_R,
  output [7:0] LEITURA
);

  wire and_1_out, and_2_out, and_3_out, and_4_out, and_5_out, and_6_out, and_7_out, and_8_out, and_9_out,
       and_10_out, and_11_out, and_12_out, and_13_out, and_14_out, and_15_out, and_16_out, and_17_out,
       and_18_out, and_19_out, and_20_out, and_21_out, and_22_out, and_23_out, and_24_out, and_25_out,
       and_26_out, and_27_out, and_28_out, and_29_out, and_30_out, and_31_out, and_32_out, and_33_out,
       and_34_out, and_35_out, and_36_out, and_37_out, and_38_out, and_39_out, and_40_out, and_41_out,
       and_42_out, and_43_out, and_44_out, and_45_out, and_46_out, and_47_out, and_48_out, and_49_out,
       and_50_out, and_51_out, and_52_out, and_53_out, and_54_out, and_55_out, and_56_out, and_57_out,
       and_58_out, and_59_out, and_60_out, and_61_out, and_62_out, and_63_out, and_64_out, and_65_out,
       and_66_out, and_67_out, and_68_out, and_69_out, and_70_out, and_71_out, and_72_out, and_73_out,
       and_74_out, and_75_out, and_76_out, and_77_out, and_78_out, and_79_out, and_80_out, d_ff_1_q,
       d_ff_2_q, d_ff_3_q, d_ff_4_q, d_ff_5_q, d_ff_6_q, d_ff_7_q, d_ff_8_q, d_ff_9_q, d_ff_10_q, d_ff_11_q,
       d_ff_12_q, d_ff_13_q, d_ff_14_q, d_ff_15_q, d_ff_16_q, d_ff_17_q, d_ff_18_q, d_ff_19_q, d_ff_20_q,
       d_ff_21_q, d_ff_22_q, d_ff_23_q, d_ff_24_q, d_ff_25_q, d_ff_26_q, d_ff_27_q, d_ff_28_q, d_ff_29_q,
       d_ff_30_q, d_ff_31_q, d_ff_32_q, d_ff_33_q, d_ff_34_q, d_ff_35_q, d_ff_36_q, d_ff_37_q, d_ff_38_q,
       d_ff_39_q, d_ff_40_q, d_ff_41_q, d_ff_42_q, d_ff_43_q, d_ff_44_q, d_ff_45_q, d_ff_46_q, d_ff_47_q,
       d_ff_48_q, d_ff_49_q, d_ff_50_q, d_ff_51_q, d_ff_52_q, d_ff_53_q, d_ff_54_q, d_ff_55_q, d_ff_56_q,
       d_ff_57_q, d_ff_58_q, d_ff_59_q, d_ff_60_q, d_ff_61_q, d_ff_62_q, d_ff_63_q, d_ff_64_q;

  and and_1 (and_1_out, ~\ENDEREÇO [2], ~\ENDEREÇO [1], ~\ENDEREÇO [0]);  // AND_Gate
  and and_2 (and_2_out, ~\ENDEREÇO [2], ~\ENDEREÇO [1], \ENDEREÇO [0]);  // AND_Gate
  and and_3 (and_3_out, ~\ENDEREÇO [2], \ENDEREÇO [1], ~\ENDEREÇO [0]);  // AND_Gate
  and and_4 (and_4_out, ~\ENDEREÇO [2], \ENDEREÇO [1], \ENDEREÇO [0]);  // AND_Gate
  and and_5 (and_5_out, \ENDEREÇO [2], ~\ENDEREÇO [1], ~\ENDEREÇO [0]);  // AND_Gate
  and and_6 (and_6_out, \ENDEREÇO [2], ~\ENDEREÇO [1], \ENDEREÇO [0]);  // AND_Gate
  and and_7 (and_7_out, \ENDEREÇO [2], \ENDEREÇO [1], ~\ENDEREÇO [0]);  // AND_Gate
  and and_8 (and_8_out, \ENDEREÇO [2], \ENDEREÇO [1], \ENDEREÇO [0]);
  and and_9 (and_9_out, and_1_out, W_R);
  and and_10 (and_10_out, and_2_out, W_R);
  and and_11 (and_11_out, and_3_out, W_R);
  and and_12 (and_12_out, and_4_out, W_R);
  and and_13 (and_13_out, and_5_out, W_R);
  and and_14 (and_14_out, and_6_out, W_R);
  and and_15 (and_15_out, and_7_out, W_R);
  and and_16 (and_16_out, and_8_out, W_R);
  D_Flip_Flop d_ff_1 (.clk(and_9_out), .D(\CONTEÚDO_A_SER_ESCRITO [7]), .Q(d_ff_1_q));  // open: Qn, preset, en, reset
  D_Flip_Flop d_ff_2 (.clk(and_10_out), .D(\CONTEÚDO_A_SER_ESCRITO [7]), .Q(d_ff_2_q));  // open: Qn, preset, en, reset
  D_Flip_Flop d_ff_3 (.clk(and_11_out), .D(\CONTEÚDO_A_SER_ESCRITO [7]), .Q(d_ff_3_q));  // open: Qn, preset, en, reset
  D_Flip_Flop d_ff_4 (.clk(and_12_out), .D(\CONTEÚDO_A_SER_ESCRITO [7]), .Q(d_ff_4_q));  // open: Qn, preset, en, reset
  D_Flip_Flop d_ff_5 (.clk(and_13_out), .D(\CONTEÚDO_A_SER_ESCRITO [7]), .Q(d_ff_5_q));  // open: Qn, preset, en, reset
  D_Flip_Flop d_ff_6 (.clk(and_14_out), .D(\CONTEÚDO_A_SER_ESCRITO [7]), .Q(d_ff_6_q));  // open: Qn, preset, en, reset
  D_Flip_Flop d_ff_7 (.clk(and_15_out), .D(\CONTEÚDO_A_SER_ESCRITO [7]), .Q(d_ff_7_q));  // open: Qn, preset, en, reset
  D_Flip_Flop d_ff_8 (.clk(and_16_out), .D(\CONTEÚDO_A_SER_ESCRITO [7]), .Q(d_ff_8_q));  // open: Qn, preset, en, reset
  and and_17 (and_17_out, d_ff_1_q, and_1_out);
  and and_18 (and_18_out, d_ff_2_q, and_2_out);
  and and_19 (and_19_out, d_ff_3_q, and_3_out);
  and and_20 (and_20_out, d_ff_4_q, and_4_out);
  and and_21 (and_21_out, d_ff_5_q, and_5_out);
  and and_22 (and_22_out, d_ff_6_q, and_6_out);
  or or_1 (LEITURA[7], and_17_out, and_18_out, and_19_out, and_20_out, and_21_out, and_22_out, and_23_out, and_24_out);
  and and_23 (and_23_out, d_ff_7_q, and_7_out);
  and and_24 (and_24_out, d_ff_8_q, and_8_out);
  D_Flip_Flop d_ff_9 (.clk(and_9_out), .D(\CONTEÚDO_A_SER_ESCRITO [6]), .Q(d_ff_9_q));  // open: Qn, preset, en, reset
  and and_25 (and_25_out, d_ff_9_q, and_1_out);
  D_Flip_Flop d_ff_10 (
    .clk(and_10_out), .D(\CONTEÚDO_A_SER_ESCRITO [6]), .Q(d_ff_10_q));  // open: Qn, preset, en, reset
  D_Flip_Flop d_ff_11 (
    .clk(and_11_out), .D(\CONTEÚDO_A_SER_ESCRITO [6]), .Q(d_ff_11_q));  // open: Qn, preset, en, reset
  D_Flip_Flop d_ff_12 (
    .clk(and_12_out), .D(\CONTEÚDO_A_SER_ESCRITO [6]), .Q(d_ff_12_q));  // open: Qn, preset, en, reset
  D_Flip_Flop d_ff_13 (
    .clk(and_13_out), .D(\CONTEÚDO_A_SER_ESCRITO [6]), .Q(d_ff_13_q));  // open: Qn, preset, en, reset
  D_Flip_Flop d_ff_14 (
    .clk(and_14_out), .D(\CONTEÚDO_A_SER_ESCRITO [6]), .Q(d_ff_14_q));  // open: Qn, preset, en, reset
  D_Flip_Flop d_ff_15 (
    .clk(and_15_out), .D(\CONTEÚDO_A_SER_ESCRITO [6]), .Q(d_ff_15_q));  // open: Qn, preset, en, reset
  D_Flip_Flop d_ff_16 (
    .clk(and_16_out), .D(\CONTEÚDO_A_SER_ESCRITO [6]), .Q(d_ff_16_q));  // open: Qn, preset, en, reset
  and and_26 (and_26_out, d_ff_10_q, and_2_out);
  and and_27 (and_27_out, d_ff_11_q, and_3_out);
  and and_28 (and_28_out, d_ff_12_q, and_4_out);
  and and_29 (and_29_out, d_ff_13_q, and_5_out);
  and and_30 (and_30_out, d_ff_14_q, and_6_out);
  and and_31 (and_31_out, d_ff_15_q, and_7_out);
  and and_32 (and_32_out, d_ff_16_q, and_8_out);
  or or_2 (LEITURA[6], and_25_out, and_26_out, and_27_out, and_28_out, and_29_out, and_30_out, and_31_out, and_32_out);
  D_Flip_Flop d_ff_17 (.clk(and_9_out), .D(\CONTEÚDO_A_SER_ESCRITO [5]), .Q(d_ff_17_q));  // open: Qn, preset, en, reset
  and and_33 (and_33_out, d_ff_17_q, and_1_out);
  D_Flip_Flop d_ff_18 (
    .clk(and_10_out), .D(\CONTEÚDO_A_SER_ESCRITO [5]), .Q(d_ff_18_q));  // open: Qn, preset, en, reset
  and and_34 (and_34_out, d_ff_18_q, and_2_out);
  D_Flip_Flop d_ff_19 (
    .clk(and_11_out), .D(\CONTEÚDO_A_SER_ESCRITO [5]), .Q(d_ff_19_q));  // open: Qn, preset, en, reset
  and and_35 (and_35_out, d_ff_19_q, and_3_out);
  D_Flip_Flop d_ff_20 (
    .clk(and_12_out), .D(\CONTEÚDO_A_SER_ESCRITO [5]), .Q(d_ff_20_q));  // open: Qn, preset, en, reset
  D_Flip_Flop d_ff_21 (
    .clk(and_13_out), .D(\CONTEÚDO_A_SER_ESCRITO [5]), .Q(d_ff_21_q));  // open: Qn, preset, en, reset
  D_Flip_Flop d_ff_22 (
    .clk(and_14_out), .D(\CONTEÚDO_A_SER_ESCRITO [5]), .Q(d_ff_22_q));  // open: Qn, preset, en, reset
  D_Flip_Flop d_ff_23 (
    .clk(and_15_out), .D(\CONTEÚDO_A_SER_ESCRITO [5]), .Q(d_ff_23_q));  // open: Qn, preset, en, reset
  D_Flip_Flop d_ff_24 (
    .clk(and_16_out), .D(\CONTEÚDO_A_SER_ESCRITO [5]), .Q(d_ff_24_q));  // open: Qn, preset, en, reset
  or or_3 (LEITURA[5], and_33_out, and_34_out, and_35_out, and_36_out, and_37_out, and_38_out, and_39_out, and_40_out);
  and and_36 (and_36_out, d_ff_20_q, and_4_out);
  and and_37 (and_37_out, d_ff_21_q, and_5_out);
  and and_38 (and_38_out, d_ff_22_q, and_6_out);
  and and_39 (and_39_out, d_ff_23_q, and_7_out);
  and and_40 (and_40_out, d_ff_24_q, and_8_out);
  D_Flip_Flop d_ff_25 (.clk(and_9_out), .D(\CONTEÚDO_A_SER_ESCRITO [4]), .Q(d_ff_25_q));  // open: Qn, preset, en, reset
  D_Flip_Flop d_ff_26 (
    .clk(and_10_out), .D(\CONTEÚDO_A_SER_ESCRITO [4]), .Q(d_ff_26_q));  // open: Qn, preset, en, reset
  D_Flip_Flop d_ff_27 (
    .clk(and_11_out), .D(\CONTEÚDO_A_SER_ESCRITO [4]), .Q(d_ff_27_q));  // open: Qn, preset, en, reset
  D_Flip_Flop d_ff_28 (
    .clk(and_12_out), .D(\CONTEÚDO_A_SER_ESCRITO [4]), .Q(d_ff_28_q));  // open: Qn, preset, en, reset
  D_Flip_Flop d_ff_29 (
    .clk(and_13_out), .D(\CONTEÚDO_A_SER_ESCRITO [4]), .Q(d_ff_29_q));  // open: Qn, preset, en, reset
  D_Flip_Flop d_ff_30 (
    .clk(and_14_out), .D(\CONTEÚDO_A_SER_ESCRITO [4]), .Q(d_ff_30_q));  // open: Qn, preset, en, reset
  D_Flip_Flop d_ff_31 (
    .clk(and_15_out), .D(\CONTEÚDO_A_SER_ESCRITO [4]), .Q(d_ff_31_q));  // open: Qn, preset, en, reset
  D_Flip_Flop d_ff_32 (
    .clk(and_16_out), .D(\CONTEÚDO_A_SER_ESCRITO [4]), .Q(d_ff_32_q));  // open: Qn, preset, en, reset
  and and_41 (and_41_out, d_ff_25_q, and_1_out);
  and and_42 (and_42_out, d_ff_26_q, and_2_out);
  and and_43 (and_43_out, d_ff_27_q, and_3_out);
  and and_44 (and_44_out, d_ff_28_q, and_4_out);
  and and_45 (and_45_out, d_ff_29_q, and_5_out);
  and and_46 (and_46_out, d_ff_30_q, and_6_out);
  or or_4 (LEITURA[4], and_41_out, and_42_out, and_43_out, and_44_out, and_45_out, and_46_out, and_47_out, and_48_out);
  and and_47 (and_47_out, d_ff_31_q, and_7_out);
  and and_48 (and_48_out, d_ff_32_q, and_8_out);
  D_Flip_Flop d_ff_33 (.clk(and_9_out), .D(\CONTEÚDO_A_SER_ESCRITO [3]), .Q(d_ff_33_q));  // open: Qn, preset, en, reset
  and and_49 (and_49_out, d_ff_33_q, and_1_out);
  D_Flip_Flop d_ff_34 (
    .clk(and_10_out), .D(\CONTEÚDO_A_SER_ESCRITO [3]), .Q(d_ff_34_q));  // open: Qn, preset, en, reset
  D_Flip_Flop d_ff_35 (
    .clk(and_11_out), .D(\CONTEÚDO_A_SER_ESCRITO [3]), .Q(d_ff_35_q));  // open: Qn, preset, en, reset
  D_Flip_Flop d_ff_36 (
    .clk(and_12_out), .D(\CONTEÚDO_A_SER_ESCRITO [3]), .Q(d_ff_36_q));  // open: Qn, preset, en, reset
  D_Flip_Flop d_ff_37 (
    .clk(and_13_out), .D(\CONTEÚDO_A_SER_ESCRITO [3]), .Q(d_ff_37_q));  // open: Qn, preset, en, reset
  D_Flip_Flop d_ff_38 (
    .clk(and_14_out), .D(\CONTEÚDO_A_SER_ESCRITO [3]), .Q(d_ff_38_q));  // open: Qn, preset, en, reset
  D_Flip_Flop d_ff_39 (
    .clk(and_15_out), .D(\CONTEÚDO_A_SER_ESCRITO [3]), .Q(d_ff_39_q));  // open: Qn, preset, en, reset
  D_Flip_Flop d_ff_40 (
    .clk(and_16_out), .D(\CONTEÚDO_A_SER_ESCRITO [3]), .Q(d_ff_40_q));  // open: Qn, preset, en, reset
  and and_50 (and_50_out, d_ff_34_q, and_2_out);
  and and_51 (and_51_out, d_ff_35_q, and_3_out);
  and and_52 (and_52_out, d_ff_36_q, and_4_out);
  and and_53 (and_53_out, d_ff_37_q, and_5_out);
  and and_54 (and_54_out, d_ff_38_q, and_6_out);
  and and_55 (and_55_out, d_ff_39_q, and_7_out);
  and and_56 (and_56_out, d_ff_40_q, and_8_out);
  or or_5 (LEITURA[3], and_49_out, and_50_out, and_51_out, and_52_out, and_53_out, and_54_out, and_55_out, and_56_out);
  D_Flip_Flop d_ff_41 (.clk(and_9_out), .D(\CONTEÚDO_A_SER_ESCRITO [2]), .Q(d_ff_41_q));  // open: Qn, preset, en, reset
  and and_57 (and_57_out, d_ff_41_q, and_1_out);
  D_Flip_Flop d_ff_42 (
    .clk(and_10_out), .D(\CONTEÚDO_A_SER_ESCRITO [2]), .Q(d_ff_42_q));  // open: Qn, preset, en, reset
  and and_58 (and_58_out, d_ff_42_q, and_2_out);
  D_Flip_Flop d_ff_43 (
    .clk(and_11_out), .D(\CONTEÚDO_A_SER_ESCRITO [2]), .Q(d_ff_43_q));  // open: Qn, preset, en, reset
  and and_59 (and_59_out, d_ff_43_q, and_3_out);
  D_Flip_Flop d_ff_44 (
    .clk(and_12_out), .D(\CONTEÚDO_A_SER_ESCRITO [2]), .Q(d_ff_44_q));  // open: Qn, preset, en, reset
  and and_60 (and_60_out, d_ff_44_q, and_4_out);
  D_Flip_Flop d_ff_45 (
    .clk(and_13_out), .D(\CONTEÚDO_A_SER_ESCRITO [2]), .Q(d_ff_45_q));  // open: Qn, preset, en, reset
  D_Flip_Flop d_ff_46 (
    .clk(and_14_out), .D(\CONTEÚDO_A_SER_ESCRITO [2]), .Q(d_ff_46_q));  // open: Qn, preset, en, reset
  D_Flip_Flop d_ff_47 (
    .clk(and_15_out), .D(\CONTEÚDO_A_SER_ESCRITO [2]), .Q(d_ff_47_q));  // open: Qn, preset, en, reset
  D_Flip_Flop d_ff_48 (
    .clk(and_16_out), .D(\CONTEÚDO_A_SER_ESCRITO [2]), .Q(d_ff_48_q));  // open: Qn, preset, en, reset
  or or_6 (LEITURA[2], and_57_out, and_58_out, and_59_out, and_60_out, and_61_out, and_62_out, and_63_out, and_64_out);
  and and_61 (and_61_out, d_ff_45_q, and_5_out);
  and and_62 (and_62_out, d_ff_46_q, and_6_out);
  and and_63 (and_63_out, d_ff_47_q, and_7_out);
  and and_64 (and_64_out, d_ff_48_q, and_8_out);
  D_Flip_Flop d_ff_49 (.clk(and_9_out), .D(\CONTEÚDO_A_SER_ESCRITO [1]), .Q(d_ff_49_q));  // open: Qn, preset, en, reset
  D_Flip_Flop d_ff_50 (
    .clk(and_10_out), .D(\CONTEÚDO_A_SER_ESCRITO [1]), .Q(d_ff_50_q));  // open: Qn, preset, en, reset
  D_Flip_Flop d_ff_51 (
    .clk(and_11_out), .D(\CONTEÚDO_A_SER_ESCRITO [1]), .Q(d_ff_51_q));  // open: Qn, preset, en, reset
  D_Flip_Flop d_ff_52 (
    .clk(and_12_out), .D(\CONTEÚDO_A_SER_ESCRITO [1]), .Q(d_ff_52_q));  // open: Qn, preset, en, reset
  D_Flip_Flop d_ff_53 (
    .clk(and_13_out), .D(\CONTEÚDO_A_SER_ESCRITO [1]), .Q(d_ff_53_q));  // open: Qn, preset, en, reset
  D_Flip_Flop d_ff_54 (
    .clk(and_14_out), .D(\CONTEÚDO_A_SER_ESCRITO [1]), .Q(d_ff_54_q));  // open: Qn, preset, en, reset
  D_Flip_Flop d_ff_55 (
    .clk(and_15_out), .D(\CONTEÚDO_A_SER_ESCRITO [1]), .Q(d_ff_55_q));  // open: Qn, preset, en, reset
  D_Flip_Flop d_ff_56 (
    .clk(and_16_out), .D(\CONTEÚDO_A_SER_ESCRITO [1]), .Q(d_ff_56_q));  // open: Qn, preset, en, reset
  and and_65 (and_65_out, d_ff_49_q, and_1_out);
  and and_66 (and_66_out, d_ff_50_q, and_2_out);
  and and_67 (and_67_out, d_ff_51_q, and_3_out);
  and and_68 (and_68_out, d_ff_52_q, and_4_out);
  and and_69 (and_69_out, d_ff_53_q, and_5_out);
  and and_70 (and_70_out, d_ff_54_q, and_6_out);
  or or_7 (LEITURA[1], and_65_out, and_66_out, and_67_out, and_68_out, and_69_out, and_70_out, and_71_out, and_72_out);
  and and_71 (and_71_out, d_ff_55_q, and_7_out);
  and and_72 (and_72_out, d_ff_56_q, and_8_out);
  D_Flip_Flop d_ff_57 (.clk(and_9_out), .D(\CONTEÚDO_A_SER_ESCRITO [0]), .Q(d_ff_57_q));  // open: Qn, preset, en, reset
  and and_73 (and_73_out, d_ff_57_q, and_1_out);
  D_Flip_Flop d_ff_58 (
    .clk(and_10_out), .D(\CONTEÚDO_A_SER_ESCRITO [0]), .Q(d_ff_58_q));  // open: Qn, preset, en, reset
  D_Flip_Flop d_ff_59 (
    .clk(and_11_out), .D(\CONTEÚDO_A_SER_ESCRITO [0]), .Q(d_ff_59_q));  // open: Qn, preset, en, reset
  D_Flip_Flop d_ff_60 (
    .clk(and_12_out), .D(\CONTEÚDO_A_SER_ESCRITO [0]), .Q(d_ff_60_q));  // open: Qn, preset, en, reset
  D_Flip_Flop d_ff_61 (
    .clk(and_13_out), .D(\CONTEÚDO_A_SER_ESCRITO [0]), .Q(d_ff_61_q));  // open: Qn, preset, en, reset
  D_Flip_Flop d_ff_62 (
    .clk(and_14_out), .D(\CONTEÚDO_A_SER_ESCRITO [0]), .Q(d_ff_62_q));  // open: Qn, preset, en, reset
  D_Flip_Flop d_ff_63 (
    .clk(and_15_out), .D(\CONTEÚDO_A_SER_ESCRITO [0]), .Q(d_ff_63_q));  // open: Qn, preset, en, reset
  D_Flip_Flop d_ff_64 (
    .clk(and_16_out), .D(\CONTEÚDO_A_SER_ESCRITO [0]), .Q(d_ff_64_q));  // open: Qn, preset, en, reset
  and and_74 (and_74_out, d_ff_58_q, and_2_out);
  and and_75 (and_75_out, d_ff_59_q, and_3_out);
  and and_76 (and_76_out, d_ff_60_q, and_4_out);
  and and_77 (and_77_out, d_ff_61_q, and_5_out);
  and and_78 (and_78_out, d_ff_62_q, and_6_out);
  and and_79 (and_79_out, d_ff_63_q, and_7_out);
  and and_80 (and_80_out, d_ff_64_q, and_8_out);
  or or_8 (LEITURA[0], and_73_out, and_74_out, and_75_out, and_76_out, and_77_out, and_78_out, and_79_out, and_80_out);
endmodule
