// Logisim project ULA.circ as structural Verilog: 11 circuits, main circuit main
module main (
  input  [7:0] A,
  input  [7:0] B,
  input  [2:0] Op,
  output [7:0] out_4,
  output [7:0] out_5
);

  wire and_1_out, and_3_out, and_4_out, and_5_out, and_6_out, and_7_out, and_8_out, not_1_out,
       somador_subtrator_2_p2;
  wire [7:0] somador_subtrator_1_resultado, undriven;

  Somador_Subtrator somador_subtrator_1 (
    .A(A), .B(B), .C__Soma_ou_subtrai(1'b0), .Resultado(somador_subtrator_1_resultado));  // open: Bit_de_sinal
  not not_1 (not_1_out, and_1_out);
  and and_1 (and_1_out, ~Op[0], ~Op[1], ~Op[2]);  // AND_Gate
  // Somador_Subtrator somador_subtrator_2: pin names not known; wires that end beside it: 1'b1, somador_subtrator_2_p2, A, B, out_5
  and and_2 (somador_subtrator_2_p2, Op[0], ~Op[1], ~Op[2]);  // AND_Gate
  and and_3 (and_3_out, ~Op[0], Op[1], ~Op[2]);  // AND_Gate
  and and_4 (and_4_out, Op[0], Op[1], ~Op[2]);  // AND_Gate
  and and_5 (and_5_out, ~Op[0], ~Op[1], Op[2]);  // AND_Gate
  and and_6 (and_6_out, Op[0], ~Op[1], Op[2]);  // AND_Gate
  and and_7 (and_7_out, ~Op[0], Op[1], Op[2]);  // AND_Gate
  and and_8 (and_8_out, Op[0], Op[1], Op[2]);
  Multiplexer #(.width(8)) multiplexer_1 (
    .in0(somador_subtrator_1_resultado), .in1(undriven), .out(out_4), .sel(not_1_out));  // open: en
  Multiplicador multiplicador_1 ();  // open: A2, B2, A1, B1, A0, B0, out_9, out_10, out_11, out_12, out_13, out_8, out_7
  SomadorRippleCarry somadorripplecarry_1 ();  // open: A, B, in_3, S

  // Notes on the sheet:
  //   Somador
  //   Subtrator
  //   Multiplicador
  //   Divisor
endmodule

module \Memória  (
  input  [7:0] \CONTEÚDO_A_SER_ESCRITO ,
  input  [2:0] \ENDEREÇO ,
  input  W_R,
  output [7:0] LEITURA
);

  wire and_1_out, and_2_out, and_3_out, and_4_out, and_5_out, and_6_out, and_7_out, and_8_out, and_9_out,
       and_10_out, and_11_out, and_12_out, and_13_out, and_14_out, and_15_out, and_16_out, and_17_out,
       and_18_out, and_19_out, and_20_out, and_21_out, and_22_out, and_23_out, and_24_out, and_25_out,
       and_26_out, and_27_out, and_28_out, and_29_out, and_30_out, and_31_out, and_32_out, and_33_out,
       and_34_out, and_35_out, and_36_out, and_37_out, and_38_out, and_39_out, and_40_out, and_41_out,
       and_42_out, and_43_out, and_44_out, and_45_out, and_46_out, and_47_out, and_48_out, and_49_out,
       and_50_out, and_51_out, and_52_out, and_53_out, and_54_out, and_55_out, and_56_out, and_57_out,
       and_58_out, and_59_out, and_60_out, and_61_out, and_62_out, and_63_out, and_64_out, and_65_out,
       and_66_out, and_67_out, and_68_out, and_69_out, and_70_out, and_71_out, and_72_out, and_73_out,
       and_74_out, and_75_out, and_76_out, and_77_out, and_78_out, and_79_out, and_80_out, d_ff_1_q,
       d_ff_2_q, d_ff_3_q, d_ff_4_q, d_ff_5_q, d_ff_6_q, d_ff_7_q, d_ff_8_q, d_ff_9_q, d_ff_10_q, d_ff_11_q,
       d_ff_12_q, d_ff_13_q, d_ff_14_q, d_ff_15_q, d_ff_16_q, d_ff_17_q, d_ff_18_q, d_ff_19_q, d_ff_20_q,
       d_ff_21_q, d_ff_22_q, d_ff_23_q, d_ff_24_q, d_ff_25_q, d_ff_26_q, d_ff_27_q, d_ff_28_q, d_ff_29_q,
       d_ff_30_q, d_ff_31_q, d_ff_32_q, d_ff_33_q, d_ff_34_q, d_ff_35_q, d_ff_36_q, d_ff_37_q, d_ff_38_q,
       d_ff_39_q, d_ff_40_q, d_ff_41_q, d_ff_42_q, d_ff_43_q, d_ff_44_q, d_ff_45_q, d_ff_46_q, d_ff_47_q,
       d_ff_48_q, d_ff_49_q, d_ff_50_q, d_ff_51_q, d_ff_52_q, d_ff_53_q, d_ff_54_q, d_ff_55_q, d_ff_56_q,
       d_ff_57_q, d_ff_58_q, d_ff_59_q, d_ff_60_q, d_ff_61_q, d_ff_62_q, d_ff_63_q, d_ff_64_q;

  and and_1 (and_1_out, ~\ENDEREÇO [2], ~\ENDEREÇO [1], ~\ENDEREÇO [0]);  // AND_Gate
  and and_2 (and_2_out, ~\ENDEREÇO [2], ~\ENDEREÇO [1], \ENDEREÇO [0]);  // AND_Gate
  and and_3 (and_3_out, ~\ENDEREÇO [2], \ENDEREÇO [1], ~\ENDEREÇO [0]);  // AND_Gate
  and and_4 (and_4_out, ~\ENDEREÇO [2], \ENDEREÇO [1], \ENDEREÇO [0]);  // AND_Gate
  and and_5 (and_5_out, \ENDEREÇO [2], ~\ENDEREÇO [1], ~\ENDEREÇO [0]);  // AND_Gate
  and and_6 (and_6_out, \ENDEREÇO [2], ~\ENDEREÇO [1], \ENDEREÇO [0]);  // AND_Gate
  and and_7 (and_7_out, \ENDEREÇO [2], \ENDEREÇO [1], ~\ENDEREÇO [0]);  // AND_Gate
  and and_8 (and_8_out, \ENDEREÇO [2], \ENDEREÇO [1], \ENDEREÇO [0]);
  and and_9 (and_9_out, and_1_out, W_R);
  and and_10 (and_10_out, and_2_out, W_R);
  and and_11 (and_11_out, and_3_out, W_R);
  and and_12 (and_12_out, and_4_out, W_R);
  and and_13 (and_13_out, and_5_out, W_R);
  and and_14 (and_14_out, and_6_out, W_R);
  and and_15 (and_15_out, and_7_out, W_R);
  and and_16 (and_16_out, and_8_out, W_R);
  D_Flip_Flop d_ff_1 (.clk(and_9_out), .D(\CONTEÚDO_A_SER_ESCRITO [7]), .Q(d_ff_1_q));  // open: Qn, preset, en, reset
  D_Flip_Flop d_ff_2 (.clk(and_10_out), .D(\CONTEÚDO_A_SER_ESCRITO [7]), .Q(d_ff_2_q));  // open: Qn, preset, en, reset
  D_Flip_Flop d_ff_3 (.clk(and_11_out), .D(\CONTEÚDO_A_SER_ESCRITO [7]), .Q(d_ff_3_q));  // open: Qn, preset, en, reset
  D_Flip_Flop d_ff_4 (.clk(and_12_out), .D(\CONTEÚDO_A_SER_ESCRITO [7]), .Q(d_ff_4_q));  // open: Qn, preset, en, reset
  D_Flip_Flop d_ff_5 (.clk(and_13_out), .D(\CONTEÚDO_A_SER_ESCRITO [7]), .Q(d_ff_5_q));  // open: Qn, preset, en, reset
  D_Flip_Flop d_ff_6 (.clk(and_14_out), .D(\CONTEÚDO_A_SER_ESCRITO [7]), .Q(d_ff_6_q));  // open: Qn, preset, en, reset
  D_Flip_Flop d_ff_7 (.clk(and_15_out), .D(\CONTEÚDO_A_SER_ESCRITO [7]), .Q(d_ff_7_q));  // open: Qn, preset, en, reset
  D_Flip_Flop d_ff_8 (.clk(and_16_out), .D(\CONTEÚDO_A_SER_ESCRITO [7]), .Q(d_ff_8_q));  // open: Qn, preset, en, reset
  and and_17 (and_17_out, d_ff_1_q, and_1_out);
  and and_18 (and_18_out, d_ff_2_q, and_2_out);
  and and_19 (and_19_out, d_ff_3_q, and_3_out);
  and and_20 (and_20_out, d_ff_4_q, and_4_out);
  and and_21 (and_21_out, d_ff_5_q, and_5_out);
  and and_22 (and_22_out, d_ff_6_q, and_6_out);
  and and_23 (and_23_out, d_ff_7_q, and_7_out);
  or or_1 (LEITURA[7], and_17_out, and_18_out, and_19_out, and_20_out, and_21_out, and_22_out, and_23_out, and_24_out);
  and and_24 (and_24_out, d_ff_8_q, and_8_out);
  D_Flip_Flop d_ff_9 (.clk(and_9_out), .D(\CONTEÚDO_A_SER_ESCRITO [6]), .Q(d_ff_9_q));  // open: Qn, preset, en, reset
  and and_25 (and_25_out, d_ff_9_q, and_1_out);
  D_Flip_Flop d_ff_10 (
    .clk(and_10_out), .D(\CONTEÚDO_A_SER_ESCRITO [6]), .Q(d_ff_10_q));  // open: Qn, preset, en, reset
  and and_26 (and_26_out, d_ff_10_q, and_2_out);
  D_Flip_Flop d_ff_11 (
    .clk(and_11_out), .D(\CONTEÚDO_A_SER_ESCRITO [6]), .Q(d_ff_11_q));  // open: Qn, preset, en, reset
  D_Flip_Flop d_ff_12 (
    .clk(and_12_out), .D(\CONTEÚDO_A_SER_ESCRITO [6]), .Q(d_ff_12_q));  // open: Qn, preset, en, reset
  D_Flip_Flop d_ff_13 (
    .clk(and_13_out), .D(\CONTEÚDO_A_SER_ESCRITO [6]), .Q(d_ff_13_q));  // open: Qn, preset, en, reset
  D_Flip_Flop d_ff_14 (
    .clk(and_14_out), .D(\CONTEÚDO_A_SER_ESCRITO [6]), .Q(d_ff_14_q));  // open: Qn, preset, en, reset
  D_Flip_Flop d_ff_15 (
    .clk(and_15_out), .D(\CONTEÚDO_A_SER_ESCRITO [6]), .Q(d_ff_15_q));  // open: Qn, preset, en, reset
  D_Flip_Flop d_ff_16 (
    .clk(and_16_out), .D(\CONTEÚDO_A_SER_ESCRITO [6]), .Q(d_ff_16_q));  // open: Qn, preset, en, reset
  and and_27 (and_27_out, d_ff_11_q, and_3_out);
  and and_28 (and_28_out, d_ff_12_q, and_4_out);
  and and_29 (and_29_out, d_ff_13_q, and_5_out);
  and and_30 (and_30_out, d_ff_14_q, and_6_out);
  and and_31 (and_31_out, d_ff_15_q, and_7_out);
  and and_32 (and_32_out, d_ff_16_q, and_8_out);
  or or_2 (LEITURA[6], and_25_out, and_26_out, and_27_out, and_28_out, and_29_out, and_30_out, and_31_out, and_32_out);
  D_Flip_Flop d_ff_17 (.clk(and_9_out), .D(\CONTEÚDO_A_SER_ESCRITO [5]), .Q(d_ff_17_q));  // open: Qn, preset, en, reset
  and and_33 (and_33_out, d_ff_17_q, and_1_out);
  D_Flip_Flop d_ff_18 (
    .clk(and_10_out), .D(\CONTEÚDO_A_SER_ESCRITO [5]), .Q(d_ff_18_q));  // open: Qn, preset, en, reset
  and and_34 (and_34_out, d_ff_18_q, and_2_out);
  D_Flip_Flop d_ff_19 (
    .clk(and_11_out), .D(\CONTEÚDO_A_SER_ESCRITO [5]), .Q(d_ff_19_q));  // open: Qn, preset, en, reset
  and and_35 (and_35_out, d_ff_19_q, and_3_out);
  D_Flip_Flop d_ff_20 (
    .clk(and_12_out), .D(\CONTEÚDO_A_SER_ESCRITO [5]), .Q(d_ff_20_q));  // open: Qn, preset, en, reset
  and and_36 (and_36_out, d_ff_20_q, and_4_out);
  D_Flip_Flop d_ff_21 (
    .clk(and_13_out), .D(\CONTEÚDO_A_SER_ESCRITO [5]), .Q(d_ff_21_q));  // open: Qn, preset, en, reset
  D_Flip_Flop d_ff_22 (
    .clk(and_14_out), .D(\CONTEÚDO_A_SER_ESCRITO [5]), .Q(d_ff_22_q));  // open: Qn, preset, en, reset
  D_Flip_Flop d_ff_23 (
    .clk(and_15_out), .D(\CONTEÚDO_A_SER_ESCRITO [5]), .Q(d_ff_23_q));  // open: Qn, preset, en, reset
  D_Flip_Flop d_ff_24 (
    .clk(and_16_out), .D(\CONTEÚDO_A_SER_ESCRITO [5]), .Q(d_ff_24_q));  // open: Qn, preset, en, reset
  or or_3 (LEITURA[5], and_33_out, and_34_out, and_35_out, and_36_out, and_37_out, and_38_out, and_39_out, and_40_out);
  and and_37 (and_37_out, d_ff_21_q, and_5_out);
  and and_38 (and_38_out, d_ff_22_q, and_6_out);
  and and_39 (and_39_out, d_ff_23_q, and_7_out);
  and and_40 (and_40_out, d_ff_24_q, and_8_out);
  D_Flip_Flop d_ff_25 (.clk(and_9_out), .D(\CONTEÚDO_A_SER_ESCRITO [4]), .Q(d_ff_25_q));  // open: Qn, preset, en, reset
  D_Flip_Flop d_ff_26 (
    .clk(and_10_out), .D(\CONTEÚDO_A_SER_ESCRITO [4]), .Q(d_ff_26_q));  // open: Qn, preset, en, reset
  D_Flip_Flop d_ff_27 (
    .clk(and_11_out), .D(\CONTEÚDO_A_SER_ESCRITO [4]), .Q(d_ff_27_q));  // open: Qn, preset, en, reset
  D_Flip_Flop d_ff_28 (
    .clk(and_12_out), .D(\CONTEÚDO_A_SER_ESCRITO [4]), .Q(d_ff_28_q));  // open: Qn, preset, en, reset
  D_Flip_Flop d_ff_29 (
    .clk(and_13_out), .D(\CONTEÚDO_A_SER_ESCRITO [4]), .Q(d_ff_29_q));  // open: Qn, preset, en, reset
  D_Flip_Flop d_ff_30 (
    .clk(and_14_out), .D(\CONTEÚDO_A_SER_ESCRITO [4]), .Q(d_ff_30_q));  // open: Qn, preset, en, reset
  D_Flip_Flop d_ff_31 (
    .clk(and_15_out), .D(\CONTEÚDO_A_SER_ESCRITO [4]), .Q(d_ff_31_q));  // open: Qn, preset, en, reset
  D_Flip_Flop d_ff_32 (
    .clk(and_16_out), .D(\CONTEÚDO_A_SER_ESCRITO [4]), .Q(d_ff_32_q));  // open: Qn, preset, en, reset
  and and_41 (and_41_out, d_ff_25_q, and_1_out);
  and and_42 (and_42_out, d_ff_26_q, and_2_out);
  and and_43 (and_43_out, d_ff_27_q, and_3_out);
  and and_44 (and_44_out, d_ff_28_q, and_4_out);
  and and_45 (and_45_out, d_ff_29_q, and_5_out);
  and and_46 (and_46_out, d_ff_30_q, and_6_out);
  and and_47 (and_47_out, d_ff_31_q, and_7_out);
  or or_4 (LEITURA[4], and_41_out, and_42_out, and_43_out, and_44_out, and_45_out, and_46_out, and_47_out, and_48_out);
  and and_48 (and_48_out, d_ff_32_q, and_8_out);
  D_Flip_Flop d_ff_33 (.clk(and_9_out), .D(\CONTEÚDO_A_SER_ESCRITO [3]), .Q(d_ff_33_q));  // open: Qn, preset, en, reset
  and and_49 (and_49_out, d_ff_33_q, and_1_out);
  D_Flip_Flop d_ff_34 (
    .clk(and_10_out), .D(\CONTEÚDO_A_SER_ESCRITO [3]), .Q(d_ff_34_q));  // open: Qn, preset, en, reset
  and and_50 (and_50_out, d_ff_34_q, and_2_out);
  D_Flip_Flop d_ff_35 (
    .clk(and_11_out), .D(\CONTEÚDO_A_SER_ESCRITO [3]), .Q(d_ff_35_q));  // open: Qn, preset, en, reset
  D_Flip_Flop d_ff_36 (
    .clk(and_12_out), .D(\CONTEÚDO_A_SER_ESCRITO [3]), .Q(d_ff_36_q));  // open: Qn, preset, en, reset
  D_Flip_Flop d_ff_37 (
    .clk(and_13_out), .D(\CONTEÚDO_A_SER_ESCRITO [3]), .Q(d_ff_37_q));  // open: Qn, preset, en, reset
  D_Flip_Flop d_ff_38 (
    .clk(and_14_out), .D(\CONTEÚDO_A_SER_ESCRITO [3]), .Q(d_ff_38_q));  // open: Qn, preset, en, reset
  D_Flip_Flop d_ff_39 (
    .clk(and_15_out), .D(\CONTEÚDO_A_SER_ESCRITO [3]), .Q(d_ff_39_q));  // open: Qn, preset, en, reset
  D_Flip_Flop d_ff_40 (
    .clk(and_16_out), .D(\CONTEÚDO_A_SER_ESCRITO [3]), .Q(d_ff_40_q));  // open: Qn, preset, en, reset
  and and_51 (and_51_out, d_ff_35_q, and_3_out);
  and and_52 (and_52_out, d_ff_36_q, and_4_out);
  and and_53 (and_53_out, d_ff_37_q, and_5_out);
  and and_54 (and_54_out, d_ff_38_q, and_6_out);
  and and_55 (and_55_out, d_ff_39_q, and_7_out);
  and and_56 (and_56_out, d_ff_40_q, and_8_out);
  or or_5 (LEITURA[3], and_49_out, and_50_out, and_51_out, and_52_out, and_53_out, and_54_out, and_55_out, and_56_out);
  D_Flip_Flop d_ff_41 (.clk(and_9_out), .D(\CONTEÚDO_A_SER_ESCRITO [2]), .Q(d_ff_41_q));  // open: Qn, preset, en, reset
  and and_57 (and_57_out, d_ff_41_q, and_1_out);
  D_Flip_Flop d_ff_42 (
    .clk(and_10_out), .D(\CONTEÚDO_A_SER_ESCRITO [2]), .Q(d_ff_42_q));  // open: Qn, preset, en, reset
  and and_58 (and_58_out, d_ff_42_q, and_2_out);
  D_Flip_Flop d_ff_43 (
    .clk(and_11_out), .D(\CONTEÚDO_A_SER_ESCRITO [2]), .Q(d_ff_43_q));  // open: Qn, preset, en, reset
  and and_59 (and_59_out, d_ff_43_q, and_3_out);
  D_Flip_Flop d_ff_44 (
    .clk(and_12_out), .D(\CONTEÚDO_A_SER_ESCRITO [2]), .Q(d_ff_44_q));  // open: Qn, preset, en, reset
  and and_60 (and_60_out, d_ff_44_q, and_4_out);
  D_Flip_Flop d_ff_45 (
    .clk(and_13_out), .D(\CONTEÚDO_A_SER_ESCRITO [2]), .Q(d_ff_45_q));  // open: Qn, preset, en, reset
  and and_61 (and_61_out, d_ff_45_q, and_5_out);
  D_Flip_Flop d_ff_46 (
    .clk(and_14_out), .D(\CONTEÚDO_A_SER_ESCRITO [2]), .Q(d_ff_46_q));  // open: Qn, preset, en, reset
  D_Flip_Flop d_ff_47 (
    .clk(and_15_out), .D(\CONTEÚDO_A_SER_ESCRITO [2]), .Q(d_ff_47_q));  // open: Qn, preset, en, reset
  D_Flip_Flop d_ff_48 (
    .clk(and_16_out), .D(\CONTEÚDO_A_SER_ESCRITO [2]), .Q(d_ff_48_q));  // open: Qn, preset, en, reset
  or or_6 (LEITURA[2], and_57_out, and_58_out, and_59_out, and_60_out, and_61_out, and_62_out, and_63_out, and_64_out);
  and and_62 (and_62_out, d_ff_46_q, and_6_out);
  and and_63 (and_63_out, d_ff_47_q, and_7_out);
  and and_64 (and_64_out, d_ff_48_q, and_8_out);
  D_Flip_Flop d_ff_49 (.clk(and_9_out), .D(\CONTEÚDO_A_SER_ESCRITO [1]), .Q(d_ff_49_q));  // open: Qn, preset, en, reset
  D_Flip_Flop d_ff_50 (
    .clk(and_10_out), .D(\CONTEÚDO_A_SER_ESCRITO [1]), .Q(d_ff_50_q));  // open: Qn, preset, en, reset
  D_Flip_Flop d_ff_51 (
    .clk(and_11_out), .D(\CONTEÚDO_A_SER_ESCRITO [1]), .Q(d_ff_51_q));  // open: Qn, preset, en, reset
  D_Flip_Flop d_ff_52 (
    .clk(and_12_out), .D(\CONTEÚDO_A_SER_ESCRITO [1]), .Q(d_ff_52_q));  // open: Qn, preset, en, reset
  D_Flip_Flop d_ff_53 (
    .clk(and_13_out), .D(\CONTEÚDO_A_SER_ESCRITO [1]), .Q(d_ff_53_q));  // open: Qn, preset, en, reset
  D_Flip_Flop d_ff_54 (
    .clk(and_14_out), .D(\CONTEÚDO_A_SER_ESCRITO [1]), .Q(d_ff_54_q));  // open: Qn, preset, en, reset
  D_Flip_Flop d_ff_55 (
    .clk(and_15_out), .D(\CONTEÚDO_A_SER_ESCRITO [1]), .Q(d_ff_55_q));  // open: Qn, preset, en, reset
  D_Flip_Flop d_ff_56 (
    .clk(and_16_out), .D(\CONTEÚDO_A_SER_ESCRITO [1]), .Q(d_ff_56_q));  // open: Qn, preset, en, reset
  and and_65 (and_65_out, d_ff_49_q, and_1_out);
  and and_66 (and_66_out, d_ff_50_q, and_2_out);
  and and_67 (and_67_out, d_ff_51_q, and_3_out);
  and and_68 (and_68_out, d_ff_52_q, and_4_out);
  and and_69 (and_69_out, d_ff_53_q, and_5_out);
  and and_70 (and_70_out, d_ff_54_q, and_6_out);
  and and_71 (and_71_out, d_ff_55_q, and_7_out);
  or or_7 (LEITURA[1], and_65_out, and_66_out, and_67_out, and_68_out, and_69_out, and_70_out, and_71_out, and_72_out);
  and and_72 (and_72_out, d_ff_56_q, and_8_out);
  D_Flip_Flop d_ff_57 (.clk(and_9_out), .D(\CONTEÚDO_A_SER_ESCRITO [0]), .Q(d_ff_57_q));  // open: Qn, preset, en, reset
  and and_73 (and_73_out, d_ff_57_q, and_1_out);
  D_Flip_Flop d_ff_58 (
    .clk(and_10_out), .D(\CONTEÚDO_A_SER_ESCRITO [0]), .Q(d_ff_58_q));  // open: Qn, preset, en, reset
  and and_74 (and_74_out, d_ff_58_q, and_2_out);
  D_Flip_Flop d_ff_59 (
    .clk(and_11_out), .D(\CONTEÚDO_A_SER_ESCRITO [0]), .Q(d_ff_59_q));  // open: Qn, preset, en, reset
  D_Flip_Flop d_ff_60 (
    .clk(and_12_out), .D(\CONTEÚDO_A_SER_ESCRITO [0]), .Q(d_ff_60_q));  // open: Qn, preset, en, reset
  D_Flip_Flop d_ff_61 (
    .clk(and_13_out), .D(\CONTEÚDO_A_SER_ESCRITO [0]), .Q(d_ff_61_q));  // open: Qn, preset, en, reset
  D_Flip_Flop d_ff_62 (
    .clk(and_14_out), .D(\CONTEÚDO_A_SER_ESCRITO [0]), .Q(d_ff_62_q));  // open: Qn, preset, en, reset
  D_Flip_Flop d_ff_63 (
    .clk(and_15_out), .D(\CONTEÚDO_A_SER_ESCRITO [0]), .Q(d_ff_63_q));  // open: Qn, preset, en, reset
  D_Flip_Flop d_ff_64 (
    .clk(and_16_out), .D(\CONTEÚDO_A_SER_ESCRITO [0]), .Q(d_ff_64_q));  // open: Qn, preset, en, reset
  and and_75 (and_75_out, d_ff_59_q, and_3_out);
  and and_76 (and_76_out, d_ff_60_q, and_4_out);
  and and_77 (and_77_out, d_ff_61_q, and_5_out);
  and and_78 (and_78_out, d_ff_62_q, and_6_out);
  and and_79 (and_79_out, d_ff_63_q, and_7_out);
  and and_80 (and_80_out, d_ff_64_q, and_8_out);
  or or_8 (LEITURA[0], and_73_out, and_74_out, and_75_out, and_76_out, and_77_out, and_78_out, and_79_out, and_80_out);
endmodule

// + -
module Somador_Subtrator (
  input  [7:0] A,
  input  [7:0] B,
  input  C__Soma_ou_subtrai,
  output [7:0] Resultado,
  output Bit_de_sinal
);

  wire and_1_out, and_2_out, and_3_out, and_4_out, and_5_out, and_6_out, and_7_out, and_8_out, and_9_out,
       and_10_out, and_11_out, and_12_out, and_13_out, and_14_out, and_15_out, and_16_out, and_17_out,
       and_18_out, and_19_out, and_20_out, and_21_out, and_22_out, and_23_out, and_24_out, and_25_out,
       and_26_out, and_27_out, and_28_out, G1_out, G2_out, G3_out, G4_out, G5_out, G6_out, GO_out, or_1_out,
       or_2_out, or_3_out, or_4_out, or_5_out, or_6_out, or_7_out, P0_out, P1_out, P2_out, P3_out, P4_out,
       P5_out, P6_out;
  wire [7:0] xor_1_out;

  assign xor_1_out = B ^ {8{C__Soma_ou_subtrai}};  // XOR_Gate xor_1, 8 bits wide
  or P0 (P0_out, A[0], xor_1_out[0]);
  and GO (GO_out, A[0], xor_1_out[0]);
  and G1 (G1_out, A[1], xor_1_out[1]);
  or P1 (P1_out, A[1], xor_1_out[1]);
  or P2 (P2_out, A[2], xor_1_out[2]);
  and G2 (G2_out, A[2], xor_1_out[2]);
  or P3 (P3_out, A[3], xor_1_out[3]);
  and G3 (G3_out, A[3], xor_1_out[3]);
  and G4 (G4_out, A[4], xor_1_out[4]);
  or P4 (P4_out, A[4], xor_1_out[4]);
  and G5 (G5_out, A[5], xor_1_out[5]);
  or P5 (P5_out, A[5], xor_1_out[5]);
  and G6 (G6_out, A[6], xor_1_out[6]);
  or P6 (P6_out, A[6], xor_1_out[6]);
  SomadorSemCOut somadorsemcout_1 (.S(Resultado[0]), .A(A[0]), .B(C__Soma_ou_subtrai), .C(xor_1_out[0]));
  and and_1 (and_1_out, P0_out, C__Soma_ou_subtrai);
  or or_1 (or_1_out, GO_out, and_1_out);
  SomadorSemCOut somadorsemcout_2 (.S(Resultado[1]), .A(A[1]), .B(or_1_out), .C(xor_1_out[1]));
  SomadorSemCOut somadorsemcout_3 (.S(Resultado[2]), .A(A[2]), .B(or_2_out), .C(xor_1_out[2]));
  and and_2 (and_2_out, GO_out, P1_out);
  and and_3 (and_3_out, P0_out, P1_out, C__Soma_ou_subtrai);
  or or_2 (or_2_out, G1_out, and_2_out, and_3_out);
  and and_4 (and_4_out, G1_out, P2_out);
  SomadorSemCOut somadorsemcout_4 (.S(Resultado[3]), .A(A[3]), .B(or_3_out), .C(xor_1_out[3]));
  and and_5 (and_5_out, GO_out, P1_out, P2_out);
  and and_6 (and_6_out, P0_out, P1_out, P2_out, C__Soma_ou_subtrai);
  or or_3 (or_3_out, G2_out, and_4_out, and_5_out, and_6_out);
  SomadorSemCOut somadorsemcout_5 (.S(Resultado[4]), .A(A[4]), .B(or_4_out), .C(xor_1_out[4]));
  and and_7 (and_7_out, G1_out, P2_out, P3_out);
  and and_8 (and_8_out, G2_out, P3_out);
  and and_9 (and_9_out, GO_out, P1_out, P2_out, P3_out);
  and and_10 (and_10_out, P0_out, P1_out, P2_out, P3_out, C__Soma_ou_subtrai);
  or or_4 (or_4_out, G2_out, and_8_out, and_7_out, and_9_out, and_10_out);
  and and_11 (and_11_out, G3_out, P4_out);
  SomadorSemCOut somadorsemcout_6 (.S(Resultado[5]), .A(A[5]), .B(or_5_out), .C(xor_1_out[5]));
  and and_12 (and_12_out, G2_out, P3_out, P4_out);
  and and_13 (and_13_out, GO_out, P1_out, P2_out, P3_out, P4_out);
  and and_14 (and_14_out, G1_out, P2_out, P3_out, P4_out);
  or or_5 (or_5_out, G4_out, and_11_out, and_12_out, and_14_out, and_13_out, and_15_out);
  and and_15 (and_15_out, P0_out, P1_out, P2_out, P3_out, P4_out, C__Soma_ou_subtrai);
  SomadorSemCOut somadorsemcout_7 (.S(Resultado[6]), .A(A[6]), .B(or_6_out), .C(xor_1_out[6]));
  and and_16 (and_16_out, G4_out, P5_out);
  and and_17 (and_17_out, G3_out, P4_out, P5_out);
  and and_18 (and_18_out, G2_out, P3_out, P4_out, P5_out);
  and and_19 (and_19_out, G1_out, P2_out, P3_out, P4_out, P5_out);
  and and_20 (and_20_out, GO_out, P1_out, P2_out, P3_out, P4_out, P5_out);
  and and_21 (and_21_out, P0_out, P1_out, P2_out, P3_out, P4_out, P5_out, C__Soma_ou_subtrai);
  or or_6 (or_6_out, G5_out, and_16_out, and_17_out, and_18_out, and_19_out, and_20_out, and_21_out);
  and and_22 (and_22_out, G5_out, P6_out);
  SomadorSemCOut somadorsemcout_8 (.S(Bit_de_sinal), .A(A[7]), .B(or_7_out), .C(xor_1_out[7]));
  and and_23 (and_23_out, G4_out, P5_out, P6_out);
  and and_24 (and_24_out, G3_out, P4_out, P5_out, P6_out);
  and and_25 (and_25_out, G2_out, P3_out, P4_out, P5_out, P6_out);
  and and_26 (and_26_out, G1_out, P2_out, P3_out, P4_out, P5_out, P6_out);
  and and_27 (and_27_out, GO_out, P1_out, P2_out, P3_out, P4_out, P5_out, P6_out);
  and and_28 (and_28_out, P0_out, P1_out, P2_out, P3_out, P4_out, P5_out, P6_out, C__Soma_ou_subtrai);
  or or_7 (or_7_out, G6_out, and_22_out, and_23_out, and_24_out, and_25_out, and_26_out, and_27_out, and_28_out);

  assign Resultado[7] = Bit_de_sinal;
endmodule

// /
module Divisor (
  input  [7:0] DIVIDENDO,
  input  [7:0] DIVISOR,
  output [7:0] RESTO,
  output [7:0] QUOCIENTE
);

  wire _0, _1, _2, _3, _4, _5, _6, _7;
  wire [7:0] multiplexer_1_out, multiplexer_2_out, multiplexer_3_out, multiplexer_4_out, multiplexer_5_out,
       multiplexer_6_out, multiplexer_7_out, somador_subtrator_1_p3, somador_subtrator_2_p3,
       somador_subtrator_3_p3, somador_subtrator_4_p3, somador_subtrator_5_p3, somador_subtrator_6_p3,
       somador_subtrator_7_p3, somador_subtrator_8_p3;

  not not_1 (QUOCIENTE[0], _0);
  not not_2 (QUOCIENTE[1], _1);
  not not_3 (QUOCIENTE[2], _2);
  not not_4 (QUOCIENTE[3], _3);
  not not_5 (QUOCIENTE[4], _4);
  not not_6 (QUOCIENTE[5], _5);
  not not_7 (QUOCIENTE[6], _6);
  not not_8 (QUOCIENTE[7], _7);
  // Somador_Subtrator somador_subtrator_1: pin names not known; wires that end beside it: _7, DIVISOR, somador_subtrator_1_p3, 1'b1, {{7{1'b0}}, DIVIDENDO[7]}
  Multiplexer #(.width(8), .enable("false")) multiplexer_1 (
    .in0(somador_subtrator_1_p3), .in1({{7{1'b0}}, DIVIDENDO[7]}), .out(multiplexer_1_out), .sel(_7));
  // Somador_Subtrator somador_subtrator_2: pin names not known; wires that end beside it: _6, DIVISOR, somador_subtrator_2_p3, 1'b1, {multiplexer_1_out[6:0], DIVIDENDO[6]}
  Multiplexer #(.width(8), .enable("false")) multiplexer_2 (
    .in0(somador_subtrator_2_p3), .in1({multiplexer_1_out[6:0], DIVIDENDO[6]}), .out(multiplexer_2_out),
    .sel(_6));
  Multiplexer #(.width(8), .enable("false")) multiplexer_3 (
    .in0(somador_subtrator_3_p3), .in1({multiplexer_2_out[6:0], DIVIDENDO[5]}), .out(multiplexer_3_out),
    .sel(_5));
  // Somador_Subtrator somador_subtrator_3: pin names not known; wires that end beside it: _5, DIVISOR, somador_subtrator_3_p3, 1'b1, {multiplexer_2_out[6:0], DIVIDENDO[5]}
  // Somador_Subtrator somador_subtrator_4: pin names not known; wires that end beside it: _4, DIVISOR, somador_subtrator_4_p3, 1'b1, {multiplexer_3_out[6:0], DIVIDENDO[4]}
  Multiplexer #(.width(8), .enable("false")) multiplexer_4 (
    .in0(somador_subtrator_4_p3), .in1({multiplexer_3_out[6:0], DIVIDENDO[4]}), .out(multiplexer_4_out),
    .sel(_4));
  // Somador_Subtrator somador_subtrator_5: pin names not known; wires that end beside it: _3, DIVISOR, somador_subtrator_5_p3, 1'b1, {multiplexer_4_out[6:0], DIVIDENDO[3]}
  Multiplexer #(.width(8), .enable("false")) multiplexer_5 (
    .in0(somador_subtrator_5_p3), .in1({multiplexer_4_out[6:0], DIVIDENDO[3]}), .out(multiplexer_5_out),
    .sel(_3));
  // Somador_Subtrator somador_subtrator_6: pin names not known; wires that end beside it: _2, DIVISOR, somador_subtrator_6_p3, 1'b1, {multiplexer_5_out[6:0], DIVIDENDO[2]}
  Multiplexer #(.width(8), .enable("false")) multiplexer_6 (
    .in0(somador_subtrator_6_p3), .in1({multiplexer_5_out[6:0], DIVIDENDO[2]}), .out(multiplexer_6_out),
    .sel(_2));
  // Somador_Subtrator somador_subtrator_7: pin names not known; wires that end beside it: _1, DIVISOR, somador_subtrator_7_p3, 1'b1, {multiplexer_6_out[6:0], DIVIDENDO[1]}
  Multiplexer #(.width(8), .enable("false")) multiplexer_7 (
    .in0(somador_subtrator_7_p3), .in1({multiplexer_6_out[6:0], DIVIDENDO[1]}), .out(multiplexer_7_out),
    .sel(_1));
  // Somador_Subtrator somador_subtrator_8: pin names not known; wires that end beside it: _0, DIVISOR, somador_subtrator_8_p3, 1'b1, {multiplexer_7_out[6:0], DIVIDENDO[0]}
  Multiplexer #(.width(8), .enable("false")) multiplexer_8 (
    .in0(somador_subtrator_8_p3), .in1({multiplexer_7_out[6:0], DIVIDENDO[0]}), .out(RESTO), .sel(_0));

  // Other names for the same wires on the sheet: D[7:0] = DIVIDENDO; DV[7:0] = DIVISOR; Q[7:0] = QUOCIENTE;
  //   R[7:0] = RESTO
endmodule

// *
module Multiplicador (
  input  A2,
  input  A1,
  input  A0,
  input  B2,
  input  B1,
  input  B0,
  output [5:0] out_7,
  output out_8,
  output out_9,
  output out_10,
  output out_11,
  output out_12,
  output out_13
);

  wire and_1_out, and_2_out, and_3_out, and_4_out, and_5_out, and_6_out, and_7_out, and_8_out,
       fulladder_2_cout, fulladder_2_s, fulladder_3_cout, halfadder_1_cout, halfadder_1_s, halfadder_2_cout,
       halfadder_3_cout;

  Hex_Digit_Display hex_digit_display_1 (.value({1'b0, A2, A1, A0}));  // open: dp
  Hex_Digit_Display hex_digit_display_2 (.value({1'b0, B2, B1, B0}));  // open: dp
  and and_1 (and_1_out, A2, B2);
  and and_2 (and_2_out, A2, B1);
  HalfAdder halfadder_1 (.A(and_2_out), .B(fulladder_2_cout), .S(halfadder_1_s), .Cout(halfadder_1_cout));
  and and_3 (and_3_out, A1, B2);
  FullAdder fulladder_1 (.A(and_1_out), .B(halfadder_1_cout), .Cin(fulladder_3_cout), .S(out_7[4]), .Cout(out_7[5]));
  and and_4 (and_4_out, A2, B0);
  and and_5 (and_5_out, A1, B1);
  FullAdder fulladder_2 (
    .A(and_5_out), .B(and_4_out), .Cin(halfadder_3_cout), .S(fulladder_2_s), .Cout(fulladder_2_cout));
  and and_6 (and_6_out, A0, B2);
  FullAdder fulladder_3 (
    .A(and_3_out), .B(halfadder_1_s), .Cin(halfadder_2_cout), .S(out_7[3]), .Cout(fulladder_3_cout));
  HalfAdder halfadder_2 (.A(and_6_out), .B(fulladder_2_s), .S(out_7[2]), .Cout(halfadder_2_cout));
  and and_7 (and_7_out, A1, B0);
  and and_8 (and_8_out, A0, B1);
  HalfAdder halfadder_3 (.A(and_8_out), .B(and_7_out), .S(out_7[1]), .Cout(halfadder_3_cout));
  and and_9 (out_7[0], A0, B0);

  assign out_8 = out_7[0];
  assign out_9 = out_7[5];
  assign out_10 = out_7[4];
  assign out_11 = out_7[3];
  assign out_12 = out_7[2];
  assign out_13 = out_7[1];

  // Notes on the sheet:
  //   X
endmodule

module SomadorRippleCarry (
  input  [7:0] A,
  input  [7:0] B,
  input  in_3,
  output [7:0] S
);

  wire somadorcomcout_2_c_out, somadorcomcout_3_c_out, somadorcomcout_4_c_out, somadorcomcout_5_c_out,
       somadorcomcout_6_c_out, somadorcomcout_7_c_out, somadorcomcout_8_c_out;
  wire [7:0] xor_1_out;

  assign xor_1_out = B ^ {8{in_3}};  // XOR_Gate xor_1, 8 bits wide
  SomadorComCOut somadorcomcout_1 (.S(S[7]), .A(A[7]), .B(xor_1_out[7]), .C(somadorcomcout_2_c_out));  // open: C_out
  SomadorComCOut somadorcomcout_2 (
    .C_out(somadorcomcout_2_c_out), .S(S[6]), .A(A[6]), .B(xor_1_out[6]), .C(somadorcomcout_3_c_out));
  SomadorComCOut somadorcomcout_3 (
    .C_out(somadorcomcout_3_c_out), .S(S[5]), .A(A[5]), .B(xor_1_out[5]), .C(somadorcomcout_4_c_out));
  SomadorComCOut somadorcomcout_4 (
    .C_out(somadorcomcout_4_c_out), .S(S[4]), .A(A[4]), .B(xor_1_out[4]), .C(somadorcomcout_5_c_out));
  SomadorComCOut somadorcomcout_5 (
    .C_out(somadorcomcout_5_c_out), .S(S[3]), .A(A[3]), .B(xor_1_out[3]), .C(somadorcomcout_6_c_out));
  SomadorComCOut somadorcomcout_6 (
    .C_out(somadorcomcout_6_c_out), .S(S[2]), .A(A[2]), .B(xor_1_out[2]), .C(somadorcomcout_7_c_out));
  SomadorComCOut somadorcomcout_7 (
    .C_out(somadorcomcout_7_c_out), .S(S[1]), .A(A[1]), .B(xor_1_out[1]), .C(somadorcomcout_8_c_out));
  SomadorComCOut somadorcomcout_8 (.C_out(somadorcomcout_8_c_out), .S(S[0]), .A(A[0]), .B(xor_1_out[0]), .C(in_3));
endmodule

module SomadorLookAhead (
  input  [7:0] A,
  input  [7:0] B,
  input  in_3,
  output [7:0] S
);

  wire and_1_out, and_2_out, and_3_out, and_4_out, and_5_out, and_6_out, and_7_out, and_8_out, and_9_out,
       and_10_out, and_11_out, and_12_out, and_13_out, and_14_out, and_15_out, and_16_out, and_17_out,
       and_18_out, and_19_out, and_20_out, and_21_out, and_22_out, and_23_out, and_24_out, and_25_out,
       and_26_out, and_27_out, and_28_out, G1_2_out, G1_out, G2_out, G3_out, G4_out, G5_out, G6_out, G7_out,
       or_1_out, or_2_out, or_3_out, or_4_out, or_5_out, or_6_out, or_7_out, P1_2_out, P1_out, P2_out,
       P3_out, P4_out, P5_out, P6_out, P7_out;
  wire [7:0] xor_1_out;

  assign xor_1_out = B ^ {8{in_3}};  // XOR_Gate xor_1, 8 bits wide
  and G1 (G1_out, A[0], xor_1_out[0]);
  or P1 (P1_out, A[0], xor_1_out[0]);
  and G1_2 (G1_2_out, A[1], xor_1_out[1]);
  or P1_2 (P1_2_out, A[1], xor_1_out[1]);
  or P2 (P2_out, A[2], xor_1_out[2]);
  and G2 (G2_out, A[2], xor_1_out[2]);
  or P3 (P3_out, A[3], xor_1_out[3]);
  and G3 (G3_out, A[3], xor_1_out[3]);
  and G4 (G4_out, A[4], xor_1_out[4]);
  and G5 (G5_out, A[5], xor_1_out[5]);
  or P4 (P4_out, A[4], xor_1_out[4]);
  or P5 (P5_out, A[5], xor_1_out[5]);
  and G6 (G6_out, A[6], xor_1_out[6]);
  or P6 (P6_out, A[6], xor_1_out[6]);
  or P7 (P7_out, A[7], xor_1_out[7]);
  and G7 (G7_out, A[7], xor_1_out[7]);
  SomadorComCOut somadorcomcout_1 (.S(S[0]), .A(A[0]), .B(xor_1_out[0]), .C(in_3));  // open: C_out
  and and_1 (and_1_out, P1_out, in_3);
  or or_1 (or_1_out, G1_out, and_1_out);
  SomadorComCOut somadorcomcout_2 (.S(S[1]), .A(A[1]), .B(xor_1_out[1]), .C(or_1_out));  // open: C_out
  SomadorComCOut somadorcomcout_3 (.S(S[2]), .A(A[2]), .B(xor_1_out[2]), .C(or_2_out));  // open: C_out
  and and_2 (and_2_out, P1_out, P1_2_out, in_3);
  and and_3 (and_3_out, G1_out, P1_2_out);
  or or_2 (or_2_out, G1_2_out, and_3_out, and_2_out);
  SomadorComCOut somadorcomcout_4 (.S(S[3]), .A(A[3]), .B(xor_1_out[3]), .C(or_3_out));  // open: C_out
  and and_4 (and_4_out, G1_2_out, P2_out);
  or or_3 (or_3_out, G2_out, and_4_out, and_5_out, and_6_out);
  and and_5 (and_5_out, G1_out, P1_2_out, P2_out);
  and and_6 (and_6_out, P1_out, P1_2_out, P2_out, in_3);
  and and_7 (and_7_out, G2_out, P3_out);
  or or_4 (or_4_out, G3_out, and_7_out, and_8_out, and_9_out, and_10_out);
  SomadorComCOut somadorcomcout_5 (.S(S[4]), .A(A[4]), .B(xor_1_out[4]), .C(or_4_out));  // open: C_out
  and and_8 (and_8_out, G1_2_out, P2_out, P3_out);
  and and_9 (and_9_out, G1_out, P1_2_out, P2_out, P3_out);
  and and_10 (and_10_out, P1_out, P1_2_out, P2_out, P3_out, in_3);
  or or_5 (or_5_out, G4_out, and_11_out, and_12_out, and_13_out, and_14_out, and_15_out);
  SomadorComCOut somadorcomcout_6 (.S(S[5]), .A(A[5]), .B(xor_1_out[5]), .C(or_5_out));  // open: C_out
  and and_11 (and_11_out, G3_out, P4_out);
  and and_12 (and_12_out, G2_out, P3_out, P4_out);
  and and_13 (and_13_out, G1_2_out, P2_out, P3_out, P4_out);
  and and_14 (and_14_out, G1_out, P1_2_out, P2_out, P3_out, P4_out);
  and and_15 (and_15_out, P1_out, P1_2_out, P2_out, P3_out, P4_out, in_3);
  SomadorComCOut somadorcomcout_7 (.S(S[6]), .A(A[6]), .B(xor_1_out[6]), .C(or_6_out));  // open: C_out
  and and_16 (and_16_out, G4_out, P5_out);
  and and_17 (and_17_out, G3_out, P4_out, P5_out);
  or or_6 (or_6_out, G5_out, and_16_out, and_17_out, and_18_out, and_19_out, and_20_out, and_21_out);
  and and_18 (and_18_out, G2_out, P3_out, P4_out, P5_out);
  and and_19 (and_19_out, G1_2_out, P2_out, P3_out, P4_out, P5_out);
  and and_20 (and_20_out, G1_out, P1_2_out, P2_out, P3_out, P4_out, P5_out);
  and and_21 (and_21_out, P1_out, P1_2_out, P2_out, P3_out, P4_out, P5_out, in_3);
  SomadorComCOut somadorcomcout_8 (.S(S[7]), .A(A[7]), .B(xor_1_out[7]), .C(or_7_out));  // open: C_out
  and and_22 (and_22_out, G5_out, P6_out);
  or or_7 (or_7_out, G6_out, and_22_out, and_23_out, and_24_out, and_25_out, and_26_out, and_27_out, and_28_out);
  and and_23 (and_23_out, G4_out, P5_out, P6_out);
  and and_24 (and_24_out, G3_out, P4_out, P5_out, P6_out);
  and and_25 (and_25_out, G2_out, P3_out, P4_out, P5_out, P6_out);
  and and_26 (and_26_out, G1_2_out, P2_out, P3_out, P4_out, P5_out, P6_out);
  and and_27 (and_27_out, G1_out, P1_2_out, P2_out, P3_out, P4_out, P5_out, P6_out);
  and and_28 (and_28_out, P1_out, P1_2_out, P2_out, P3_out, P4_out, P5_out, P6_out, in_3);

  // Notes on the sheet:
  //   C out 0
  //   C out 1
  //   C out 2
  //   C out 3
  //   C out 4
  //   C out 5
  //   C out 6
endmodule

module SomadorComCOut (
  input  A,
  input  B,
  input  C,
  output C_out,
  output S
);

  wire and_1_out, and_2_out, and_3_out, xor_1_out;

  and and_1 (and_1_out, A, B);
  and and_2 (and_2_out, A, C);
  or or_1 (C_out, and_1_out, and_2_out, and_3_out);
  and and_3 (and_3_out, B, C);
  xor xor_1 (xor_1_out, B, C);
  xor xor_2 (S, xor_1_out, A);
endmodule

module SomadorSemCOut (
  input  A,
  input  B,
  input  C,
  output S
);

  wire xor_1_out;

  xor xor_1 (xor_1_out, C, B);
  xor xor_2 (S, xor_1_out, A);
endmodule

module FullAdder (
  input  A,
  input  B,
  input  Cin,
  output S,
  output Cout
);

  wire and_1_out, and_2_out, and_3_out, and_4_out, and_5_out, and_6_out, not_1_out, not_2_out, not_3_out,
       not_4_out, not_5_out, not_6_out;

  not not_1 (not_1_out, A);
  not not_2 (not_2_out, B);
  not not_3 (not_3_out, A);
  not not_4 (not_4_out, Cin);
  not not_5 (not_5_out, B);
  not not_6 (not_6_out, Cin);
  and and_1 (and_1_out, A, Cin);
  and and_2 (and_2_out, A, B);
  and and_3 (and_3_out, not_1_out, not_2_out, Cin);
  and and_4 (and_4_out, not_3_out, B, not_4_out);
  and and_5 (and_5_out, A, not_5_out, not_6_out);
  and and_6 (and_6_out, A, B, Cin);
  or or_1 (Cout, and_1_out, and_2_out);
  or or_2 (S, and_3_out, and_4_out, and_5_out, and_6_out);
endmodule

module HalfAdder (
  input  A,
  input  B,
  output S,
  output Cout
);

  wire and_2_out, and_3_out, not_1_out, not_2_out;

  not not_1 (not_1_out, A);
  not not_2 (not_2_out, B);
  and and_1 (Cout, A, B);
  and and_2 (and_2_out, not_1_out, B);
  and and_3 (and_3_out, A, not_2_out);
  or or_1 (S, and_2_out, and_3_out);
endmodule
