// Logisim project lista02.circ as structural Verilog: 1 circuit, main circuit main
module main (
  input  A,
  input  B,
  input  C,
  input  D,
  output out_5,
  output out_6
);

  wire and_1_out, and_2_out, nand_1_out, nor_1_out, not_1_out, not_2_out, not_3_out, not_4_out, not_5_out,
       not_6_out, not_7_out, not_8_out, not_9_out, or_1_out, or_2_out, xor_1_out;

  not not_1 (not_1_out, B);
  not not_2 (not_2_out, D);
  not not_3 (not_3_out, A);
  not not_4 (not_4_out, C);
  not not_5 (not_5_out, A);
  not not_6 (not_6_out, D);
  not not_7 (not_7_out, D);
  not not_8 (not_8_out, B);
  not not_9 (not_9_out, D);
  ExactlyOne xor_1 (.out(xor_1_out), .in0(A), .in1(not_1_out), .in2(C));
  or or_1 (or_1_out, A, not_2_out, B);
  and and_1 (and_1_out, B, C);
  and and_2 (and_2_out, not_8_out, D);
  or or_2 (or_2_out, and_2_out, not_9_out);
  nand nand_1 (nand_1_out, xor_1_out, or_1_out);
  nor nor_1 (nor_1_out, not_5_out, and_1_out, not_6_out);
  or or_3 (out_6, nor_1_out, not_7_out, or_2_out);
  and and_3 (out_5, nand_1_out, not_3_out, B, not_4_out);

  // Notes on the sheet:
  //   Ex 08
  //   Ex 09
endmodule
